// Logisim project (2^n)mod5.circ as structural Verilog: 3 circuits, main circuit 拆分
module \拆分  (
  input  [1:0] in_1,
  input  in_2,
  output [1:0] out_3
);


  assign out_3 = {in_1[0], in_2};
endmodule

module \取模  (
  input  [1:0] in_1,
  output ans0,
  output ans1,
  output ans2,
  output ans3,
  output ans4
);

  wire not_1_out, not_2_out, not_3_out, not_4_out;

  not not_1 (not_1_out, in_1[1]);
  not not_2 (not_2_out, in_1[0]);
  not not_3 (not_3_out, in_1[1]);
  and and_1 (ans3, in_1[1], in_1[0]);
  not not_4 (not_4_out, in_1[0]);
  and and_2 (ans1, not_1_out, not_2_out);
  and and_3 (ans2, not_3_out, in_1[0]);
  and and_4 (ans4, in_1[1], not_4_out);

  assign ans0 = 1'b0;
endmodule

module mod5 (
  input  in_1,
  output out_2,
  output out_3,
  output out_4,
  output out_5,
  output out_6
);

  wire clock_1_out;
  wire [1:0] register_1_q, \拆分_1_out_3 ;

  // Probe on register_1_q
  \拆分  \u_拆分_1  (.in_1(register_1_q), .in_2(in_1), .out_3(\拆分_1_out_3 ));
  // Probe on register_1_q
  Register #(.width(2)) register_1 (.D(\拆分_1_out_3 ), .Q(register_1_q), .clk(clock_1_out));  // open: en, clr
  Clock clock_1 (.out(clock_1_out));
  \取模  \u_取模_1  (.in_1(register_1_q), .ans0(out_2), .ans1(out_3), .ans2(out_4), .ans3(out_5), .ans4(out_6));
endmodule
