// Logisim project 算数右移.circ as structural Verilog: 1 circuit, main circuit main
module main (
  input  [15:0] in_1,
  input  [3:0] in_2,
  output [15:0] out_3
);

  wire \移位0 , \移位1 , \移位2 , \移位3 ;
  wire [15:0] multiplexer_1_out, multiplexer_2_out, multiplexer_3_out;

  not not_1 (\移位0 , in_2[0]);
  not not_2 (\移位1 , in_2[1]);
  not not_3 (\移位2 , in_2[2]);
  not not_4 (\移位3 , in_2[3]);
  Multiplexer #(.width(16)) multiplexer_1 (
    .in0({{2{in_1[15]}}, in_1[14:1]}), .in1(in_1), .out(multiplexer_1_out), .sel(\移位0 ));  // open: en
  Multiplexer #(.width(16)) multiplexer_2 (
    .in0({{2{in_1[15]}}, multiplexer_1_out[15:2]}), .in1(multiplexer_1_out), .out(multiplexer_2_out),
    .sel(\移位1 ));  // open: en
  Multiplexer #(.width(16)) multiplexer_3 (
    .in0({{4{in_1[15]}}, multiplexer_2_out[15:4]}), .in1(multiplexer_2_out), .out(multiplexer_3_out),
    .sel(\移位2 ));  // open: en
  Multiplexer #(.width(16)) multiplexer_4 (
    .in0({{8{in_1[15]}}, multiplexer_3_out[15:8]}), .in1(multiplexer_3_out), .out(out_3), .sel(\移位3 ));  // open: en

  // Other names for the same wires on the sheet: 输入[15:0] = in_1; 符号位 = in_1[15]
endmodule
