// Logisim project 饮料机.circ as structural Verilog: 3 circuits, main circuit main
module main (
  input  [2:0] in_1,
  output [2:0] out_2,
  output out_3
);

  wire clock_1_out;
  wire [3:0] register_1_q, \状态转移_1_out_3 ;

  \状态转移  \u_状态转移_1  (.in_1(register_1_q), .in_2(in_1), .out_3(\状态转移_1_out_3 ));
  Register #(.width(4)) register_1 (.D(\状态转移_1_out_3 ), .Q(register_1_q), .clk(clock_1_out));  // open: en, clr
  Clock clock_1 (.out(clock_1_out));
  \输出  \u_输出_1  (.in_1(register_1_q), .out_2(out_2), .out_3(out_3));
endmodule

module \状态转移  (
  input  [3:0] in_1,
  input  [2:0] in_2,
  output [3:0] out_3
);

  wire comparator_1_eq, comparator_1_gt, flag;
  wire [3:0] bit_extender_1_out, status;

  Multiplexer #(.width(4)) multiplexer_1 (.in0(in_1), .in1(4'b0000), .out(status), .sel(flag));  // open: en
  assign bit_extender_1_out = {{1{1'b0}}, in_2};  // Bit_Extender bit_extender_1
  Comparator #(.width(4), .mode("unsigned")) comparator_1 (
    .a(in_1), .b(4'b0101), .gt(comparator_1_gt), .eq(comparator_1_eq));  // open: lt
  Adder #(.width(4)) adder_1 (.a(status), .b(bit_extender_1_out), .out(out_3));  // open: cin, cout
  or or_1 (flag, comparator_1_gt, comparator_1_eq);
endmodule

module \输出  (
  input  [3:0] in_1,
  output [2:0] out_2,
  output out_3
);

  wire comparator_1_eq, comparator_1_gt;
  wire [3:0] multiplexer_1_out, subtractor_1_out;

  Comparator #(.width(4), .mode("unsigned")) comparator_1 (
    .a(in_1), .b(4'b0101), .gt(comparator_1_gt), .eq(comparator_1_eq));  // open: lt
  Subtractor #(.width(4)) subtractor_1 (.a(in_1), .b(4'b0101), .out(subtractor_1_out));  // open: bin, bout
  or or_1 (out_3, comparator_1_gt, comparator_1_eq);
  Multiplexer #(.width(4)) multiplexer_1 (
    .in0(4'b0000), .in1(subtractor_1_out), .out(multiplexer_1_out), .sel(out_3));  // open: en
  Bit_Extender #(.in_width(4), .out_width(3)) bit_extender_1 (.in(multiplexer_1_out), .out(out_2));
endmodule
