// Logisim project 2021字符串状态机.circ as structural Verilog: 3 circuits, main circuit main
module main (
  input  [1:0] in_1,
  output [1:0] out_2
);

  wire undriven;
  wire [2:0] register_1_q, \状态转移_1_out_3 ;

  \状态转移  \u_状态转移_1  (.in_1(register_1_q), .in_2(in_1), .out_3(\状态转移_1_out_3 ));
  Clock clock_1 ();  // open: out
  Register #(.width(3)) register_1 (.D(\状态转移_1_out_3 ), .Q(register_1_q), .clk(undriven));  // open: en, clr
  \输出  \u_输出_1  (.in_1(register_1_q), .in_2(in_1), .out_3(out_2));
endmodule

module \状态转移  (
  input  [2:0] in_1,
  input  [1:0] in_2,
  output [2:0] out_3
);

  wire and_1_out, and_2_out, and_3_out, and_4_out, and_5_out, and_6_out, and_7_out, and_8_out, and_9_out,
       not_1_out, not_2_out, not_3_out, not_4_out, not_5_out, not_6_out, not_7_out, not_8_out, not_9_out,
       not_10_out;

  not not_1 (not_1_out, in_1[0]);
  not not_2 (not_2_out, in_2[1]);
  not not_3 (not_3_out, in_1[1]);
  not not_4 (not_4_out, in_2[1]);
  not not_5 (not_5_out, in_2[0]);
  not not_6 (not_6_out, in_1[0]);
  not not_7 (not_7_out, in_2[1]);
  not not_8 (not_8_out, in_1[1]);
  not not_9 (not_9_out, in_2[0]);
  not not_10 (not_10_out, in_2[1]);
  and and_1 (and_1_out, in_1[1], not_1_out, in_2[1]);
  and and_2 (and_2_out, in_1[1], in_1[0], not_2_out, in_2[0]);
  and and_3 (and_3_out, in_1[2], in_2[0]);
  and and_4 (and_4_out, not_3_out, in_1[0], not_4_out, not_5_out);
  and and_5 (and_5_out, in_1[1], not_6_out, in_2[0]);
  and and_6 (and_6_out, in_1[2], not_7_out);
  and and_7 (and_7_out, not_8_out, in_2[1]);
  and and_8 (and_8_out, in_1[0], in_2[1], not_9_out);
  or or_1 (out_3[0], and_7_out, and_8_out, and_9_out);
  and and_9 (and_9_out, in_1[1], not_10_out, in_2[0]);
  or or_2 (out_3[2], and_1_out, and_2_out, and_3_out);
  or or_3 (out_3[1], and_4_out, and_5_out, and_6_out);
endmodule

module \输出  (
  input  [2:0] in_1,
  input  [1:0] in_2,
  output [1:0] out_3
);

  wire not_1_out, not_2_out, not_3_out, not_4_out, not_5_out;

  not not_1 (not_1_out, in_1[1]);
  not not_2 (not_2_out, in_1[0]);
  not not_3 (not_3_out, in_2[1]);
  not not_4 (not_4_out, in_1[2]);
  not not_5 (not_5_out, in_2[1]);
  and and_1 (out_3[1], in_1[2], not_1_out, not_2_out, not_3_out, in_2[0]);
  and and_2 (out_3[0], not_4_out, in_1[1], in_1[0], not_5_out, in_2[0]);
endmodule
