// Logisim project 2^xmod5.circ as structural Verilog: 3 circuits, main circuit change
module change (
  input  [1:0] in_1,
  input  c,
  output [1:0] out_3
);


  assign out_3 = {in_1[0], c};
endmodule

module mod (
  input  [1:0] in_1,
  input  c,
  output x,
  output y,
  output z,
  output u,
  output v
);

  wire not_1_out, not_2_out, not_3_out, not_4_out;

  not not_1 (not_1_out, in_1[0]);
  not not_2 (not_2_out, c);
  not not_3 (not_3_out, in_1[0]);
  and and_1 (u, in_1[0], c);
  not not_4 (not_4_out, c);
  and and_2 (y, not_1_out, not_2_out);
  and and_3 (z, not_3_out, c);
  and and_4 (v, in_1[0], not_4_out);

  assign x = 1'b0;
endmodule

module mod5 (
  input  in_1,
  output out_2,
  output out_3,
  output out_4,
  output out_5,
  output out_6
);

  wire clock_1_out;
  wire [1:0] change_1_out_3, register_1_q;

  change change_1 (.in_1(register_1_q), .c(in_1), .out_3(change_1_out_3));
  Clock clock_1 (.out(clock_1_out));
  Register #(.width(2)) register_1 (.D(change_1_out_3), .Q(register_1_q), .clk(clock_1_out));  // open: en, clr
  // Probe on register_1_q
  mod mod_1 (.in_1(register_1_q), .c(in_1), .x(out_2), .y(out_3), .z(out_4), .u(out_5), .v(out_6));
endmodule
