// Logisim project 2的n次方mod5.circ as structural Verilog
module shifter (
  input  [1:0] in_1,
  input  b,
  output [1:0] out_3
);


  assign out_3 = {in_1[0], b};
endmodule
