// Logisim project CRC.circ as structural Verilog: 4 circuits, main circuit 除法
module \除法  (
  input  [10:0] in_1,
  input  [3:0] in_2,
  output [2:0] out_3
);

  wire [2:0] \四位模二除法_1_out_3 , \四位模二除法_2_out_3 , \四位模二除法_3_out_3 , \四位模二除法_4_out_3 , \四位模二除法_7_out_3 , \阶段1 ;
  wire [3:1] \四位模二除法_6_out_3 ;

  // Probe on in_1[10:7]
  // Probe on \四位模二除法_1_out_3 
  \四位模二除法  \u_四位模二除法_1  (.in_1(in_1[10:7]), .in_2(in_2), .out_3(\四位模二除法_1_out_3 ));
  \四位模二除法  \u_四位模二除法_2  (.in_1({\阶段1 , in_1[2]}), .in_2(in_2), .out_3(\四位模二除法_2_out_3 ));
  // Probe on {\四位模二除法_1_out_3 , in_1[6]}
  \四位模二除法  \u_四位模二除法_3  (.in_1({\四位模二除法_2_out_3 , in_1[1]}), .in_2(in_2), .out_3(\四位模二除法_3_out_3 ));
  // Probe on \四位模二除法_4_out_3 
  \四位模二除法  \u_四位模二除法_4  (.in_1({\四位模二除法_1_out_3 , in_1[6]}), .in_2(in_2), .out_3(\四位模二除法_4_out_3 ));
  // Probe on {\四位模二除法_4_out_3 , in_1[5]}
  \四位模二除法  \u_四位模二除法_5  (.in_1({\四位模二除法_3_out_3 , in_1[0]}), .in_2(in_2), .out_3(out_3));
  \四位模二除法  \u_四位模二除法_6  (.in_1({\四位模二除法_4_out_3 , in_1[5]}), .in_2(in_2), .out_3(\四位模二除法_6_out_3 ));
  // Probe on \四位模二除法_6_out_3 
  \四位模二除法  \u_四位模二除法_7  (.in_1({\四位模二除法_6_out_3 , in_1[4]}), .in_2(in_2), .out_3(\四位模二除法_7_out_3 ));
  // Probe on \四位模二除法_7_out_3 
  \四位模二除法  \u_四位模二除法_8  (.in_1({\四位模二除法_7_out_3 , in_1[3]}), .in_2(in_2), .out_3(\阶段1 ));

  // Other names for the same wires on the sheet: a7 = in_1[7]; a8 = in_1[8]; a9 = in_1[9]; a10 = in_1[10];
  //   a2 = in_1[2]; a1 = in_1[1]; a6 = in_1[6]; a0 = in_1[0]; a5 = in_1[5]; a4 = in_1[4]; a3 = in_1[3];
  //   除数[3:0] = in_2
endmodule

module \四位模二除法  (
  input  [3:0] in_1,
  input  [3:0] in_2,
  output [2:0] out_3
);

  wire [3:0] multiplexer_1_out, xor_1_out;

  // Probe on xor_1_out
  assign xor_1_out = in_1 ^ in_2;  // XOR_Gate xor_1, 4 bits wide
  Multiplexer #(.width(4)) multiplexer_1 (
    .in0(in_1), .in1(xor_1_out), .out(multiplexer_1_out), .sel(in_1[3]));  // open: en
  Bit_Extender #(.in_width(4), .out_width(3)) bit_extender_1 (.in(multiplexer_1_out), .out(out_3));

  // Other names for the same wires on the sheet: a1[3:0] = in_1; flag = in_1[3]; a2[3:0] = in_2
endmodule

module CRC (
  input  [7:0] in_1,
  input  [3:0] in_2,
  output [10:0] out_3
);

  wire [10:0] \扩增_1_out_2 ;

  \扩增  \u_扩增_1  (.in_1(in_1), .out_2(\扩增_1_out_2 ));
  // Probe on \扩增_1_out_2 
  \除法  \u_除法_1  (.in_1(\扩增_1_out_2 ), .in_2(in_2), .out_3(out_3[2:0]));

  assign out_3[10:3] = in_1;
endmodule

module \扩增  (
  input  [7:0] in_1,
  output [10:0] out_2
);


  assign out_2 = {in_1, 3'b000};
endmodule
