// Logisim project GRF.circ as structural Verilog: 2 circuits, main circuit grf
module grf (
  input  clk,
  input  reset,
  input  WE,
  input  [4:0] A1,
  input  [4:0] A2,
  input  [4:0] A3,
  input  [31:0] WD,
  output [31:0] out_8,
  output [31:0] out_9
);

  wire [31:0] _0, _1, _2, _3, _4, _5, _6, _7, _8, _9, _10, _11, _12, _13, _14, _15, _16, _17, _18, _19, _20,
       _21, _22, _23, _24, _25, _26, _27, _28, _29, _30, _31, o1, o2, o3, o4, o5, o6, o7, o8, o9, o10, o11,
       o12, o13, o14, o15, o16, o17, o18, o19, o20, o21, o22, o23, o24, o25, o26, o27, o28, o29, o30, o31;

  Demultiplexer #(.select(5), .width(32), .tristate("true")) demultiplexer_1 (
    .out1(_1), .out2(_2), .out3(_3), .out4(_4), .out5(_5), .out6(_6), .out7(_7), .out8(_8), .out9(_9),
    .out10(_10), .out11(_11), .out12(_12), .out13(_13), .out14(_14), .out15(_15), .out16(_16), .out17(_17),
    .out18(_18), .out19(_19), .out20(_20), .out21(_21), .out22(_22), .out23(_23), .out24(_24), .out25(_25),
    .out26(_26), .out27(_27), .out28(_28), .out29(_29), .out30(_30), .out31(_31), .in(WD), .sel(A3));  // open: out0, en
  Register #(.width(32)) register_1 (.D({32{1'b0}}), .en(WE), .Q(_0), .clk(clk), .clr(reset));
  \reg  reg_1 (.in_1(_4), .in_2(WE), .in_3(clk), .in_4(reset), .out_5(o4));
  \reg  reg_2 (.in_1(_8), .in_2(WE), .in_3(clk), .in_4(reset), .out_5(o8));
  \reg  reg_3 (.in_1(_12), .in_2(WE), .in_3(clk), .in_4(reset), .out_5(o12));
  \reg  reg_4 (.in_1(_16), .in_2(WE), .in_3(clk), .in_4(reset), .out_5(o16));
  \reg  reg_5 (.in_1(_20), .in_2(WE), .in_3(clk), .in_4(reset), .out_5(o20));
  \reg  reg_6 (.in_1(_24), .in_2(WE), .in_3(clk), .in_4(reset), .out_5(o24));
  \reg  reg_7 (.in_1(_28), .in_2(WE), .in_3(clk), .in_4(reset), .out_5(o28));
  Register #(.width(32)) register_2 (.D(_1), .en(WE), .Q(o1), .clk(clk), .clr(reset));
  \reg  reg_8 (.in_1(_5), .in_2(WE), .in_3(clk), .in_4(reset), .out_5(o5));
  \reg  reg_9 (.in_1(_9), .in_2(WE), .in_3(clk), .in_4(reset), .out_5(o9));
  \reg  reg_10 (.in_1(_13), .in_2(WE), .in_3(clk), .in_4(reset), .out_5(o13));
  \reg  reg_11 (.in_1(_17), .in_2(WE), .in_3(clk), .in_4(reset), .out_5(o17));
  \reg  reg_12 (.in_1(_21), .in_2(WE), .in_3(clk), .in_4(reset), .out_5(o21));
  \reg  reg_13 (.in_1(_25), .in_2(WE), .in_3(clk), .in_4(reset), .out_5(o25));
  \reg  reg_14 (.in_1(_29), .in_2(WE), .in_3(clk), .in_4(reset), .out_5(o29));
  \reg  reg_15 (.in_1(_2), .in_2(WE), .in_3(clk), .in_4(reset), .out_5(o2));
  \reg  reg_16 (.in_1(_6), .in_2(WE), .in_3(clk), .in_4(reset), .out_5(o6));
  \reg  reg_17 (.in_1(_10), .in_2(WE), .in_3(clk), .in_4(reset), .out_5(o10));
  \reg  reg_18 (.in_1(_14), .in_2(WE), .in_3(clk), .in_4(reset), .out_5(o14));
  \reg  reg_19 (.in_1(_18), .in_2(WE), .in_3(clk), .in_4(reset), .out_5(o18));
  \reg  reg_20 (.in_1(_22), .in_2(WE), .in_3(clk), .in_4(reset), .out_5(o22));
  \reg  reg_21 (.in_1(_26), .in_2(WE), .in_3(clk), .in_4(reset), .out_5(o26));
  \reg  reg_22 (.in_1(_30), .in_2(WE), .in_3(clk), .in_4(reset), .out_5(o30));
  \reg  reg_23 (.in_1(_3), .in_2(WE), .in_3(clk), .in_4(reset), .out_5(o3));
  \reg  reg_24 (.in_1(_7), .in_2(WE), .in_3(clk), .in_4(reset), .out_5(o7));
  \reg  reg_25 (.in_1(_11), .in_2(WE), .in_3(clk), .in_4(reset), .out_5(o11));
  \reg  reg_26 (.in_1(_15), .in_2(WE), .in_3(clk), .in_4(reset), .out_5(o15));
  \reg  reg_27 (.in_1(_19), .in_2(WE), .in_3(clk), .in_4(reset), .out_5(o19));
  \reg  reg_28 (.in_1(_23), .in_2(WE), .in_3(clk), .in_4(reset), .out_5(o23));
  \reg  reg_29 (.in_1(_27), .in_2(WE), .in_3(clk), .in_4(reset), .out_5(o27));
  \reg  reg_30 (.in_1(_31), .in_2(WE), .in_3(clk), .in_4(reset), .out_5(o31));
  Multiplexer #(.select(5), .width(32)) multiplexer_1 (
    .in0(_0), .in1(o1), .in2(o2), .in3(o3), .in4(o4), .in5(o5), .in6(o6), .in7(o7), .in8(o8), .in9(o9),
    .in10(o10), .in11(o11), .in12(o12), .in13(o13), .in14(o14), .in15(o15), .in16(o16), .in17(o17),
    .in18(o18), .in19(o19), .in20(o20), .in21(o21), .in22(o22), .in23(o23), .in24(o24), .in25(o25),
    .in26(o26), .in27(o27), .in28(o28), .in29(o29), .in30(o30), .in31(o31), .out(out_8), .sel(A1));  // open: en
  Multiplexer #(.select(5), .width(32)) multiplexer_2 (
    .in0(_0), .in1(o1), .in2(o2), .in3(o3), .in4(o4), .in5(o5), .in6(o6), .in7(o7), .in8(o8), .in9(o9),
    .in10(o10), .in11(o11), .in12(o12), .in13(o13), .in14(o14), .in15(o15), .in16(o16), .in17(o17),
    .in18(o18), .in19(o19), .in20(o20), .in21(o21), .in22(o22), .in23(o23), .in24(o24), .in25(o25),
    .in26(o26), .in27(o27), .in28(o28), .in29(o29), .in30(o30), .in31(o31), .out(out_9), .sel(A2));  // open: en
endmodule

module \reg  (
  input  [31:0] in_1,
  input  in_2,
  input  in_3,
  input  in_4,
  output [31:0] out_5
);

  // Probe on in_1
  Register #(.width(32)) register_1 (.D(in_1), .en(in_2), .Q(out_5), .clk(in_3), .clr(in_4));

  // Other names for the same wires on the sheet: a[31:0] = in_1; b[31:0] = out_5
endmodule
