// Logisim project P0.circ as structural Verilog: 1 circuit, main circuit main
module main (
  input  [1:0] in_1,
  input  [1:0] in_2,
  input  [1:0] in_3,
  input  [1:0] in_4
);

  wire comparator_2_eq, comparator_3_eq, comparator_4_eq, comparator_5_eq, comparator_6_eq, comparator_7_eq,
       comparator_8_eq, comparator_9_eq, \是否一票否决 ;
  wire [2:0] agree1, agree2, agree3, agreeleader, disagree1, disagree2, disagree3, disagreeleader;

  Comparator #(.width(2), .mode("unsigned")) comparator_1 (.a(2'b10), .b(in_1), .eq(\是否一票否决 ));  // open: gt, lt
  Comparator #(.width(2), .mode("unsigned")) comparator_2 (.a(2'b00), .b(in_2), .eq(comparator_2_eq));  // open: gt, lt
  Comparator #(.width(2), .mode("unsigned")) comparator_3 (.a(2'b10), .b(in_2), .eq(comparator_3_eq));  // open: gt, lt
  Comparator #(.width(2), .mode("unsigned")) comparator_4 (.a(2'b00), .b(in_3), .eq(comparator_4_eq));  // open: gt, lt
  Comparator #(.width(2), .mode("unsigned")) comparator_5 (.a(2'b10), .b(in_3), .eq(comparator_5_eq));  // open: gt, lt
  Comparator #(.width(2), .mode("unsigned")) comparator_6 (.a(2'b00), .b(in_4), .eq(comparator_6_eq));  // open: gt, lt
  Comparator #(.width(2), .mode("unsigned")) comparator_7 (.a(2'b10), .b(in_4), .eq(comparator_7_eq));  // open: gt, lt
  Comparator #(.width(2), .mode("unsigned")) comparator_8 (.a(2'b00), .b(in_1), .eq(comparator_8_eq));  // open: gt, lt
  Comparator #(.width(2), .mode("unsigned")) comparator_9 (.a(2'b11), .b(in_1), .eq(comparator_9_eq));  // open: gt, lt
  assign disagree1 = {{2{1'b0}}, comparator_2_eq};  // Bit_Extender bit_extender_1
  assign agree1 = {{2{1'b0}}, comparator_3_eq};  // Bit_Extender bit_extender_2
  assign disagree2 = {{2{1'b0}}, comparator_4_eq};  // Bit_Extender bit_extender_3
  assign agree2 = {{2{1'b0}}, comparator_5_eq};  // Bit_Extender bit_extender_4
  assign disagree3 = {{2{1'b0}}, comparator_6_eq};  // Bit_Extender bit_extender_5
  assign agree3 = {{2{1'b0}}, comparator_7_eq};  // Bit_Extender bit_extender_6
  assign disagreeleader = {{2{1'b0}}, comparator_8_eq};  // Bit_Extender bit_extender_7
  assign agreeleader = {{2{1'b0}}, comparator_9_eq};  // Bit_Extender bit_extender_8

  // Other names for the same wires on the sheet: leader[1:0] = in_1; player1[1:0] = in_2; player2[1:0] = in_3;
  //   player3[1:0] = in_4
endmodule
