// Logisim project P1折腾版.circ as structural Verilog: 10 circuits, main circuit main
module Control (
  input  [5:0] \function ,
  input  [5:0] opcode,
  input  in_3,
  output lwor,
  output [1:0] NPCOp,
  output [1:0] WRSel,
  output [1:0] WDSel,
  output RFWr,
  output EXTOp,
  output BSel,
  output [2:0] ALUOp,
  output DMWr,
  output [1:0] DMsel
);

  wire add, beq, bezal, bezal_1, bezal_2, j, jal, jr, lb, lh, lui, lw, not_1_out, not_2_out, not_3_out,
       not_4_out, not_5_out, not_6_out, not_7_out, not_8_out, not_9_out, not_10_out, not_11_out, not_12_out,
       not_13_out, ori, sb, sh, sll, slo, special, sub, sw;

  not not_1 (not_1_out, opcode[5]);
  not not_2 (not_2_out, opcode[4]);
  not not_3 (not_3_out, opcode[3]);
  not not_4 (not_4_out, opcode[2]);
  not not_5 (not_5_out, opcode[0]);
  not not_6 (not_6_out, opcode[1]);
  and u_special (special, not_1_out, not_2_out, not_3_out, not_4_out, not_6_out, not_5_out);
  and u_ori (ori, not_1_out, not_2_out, opcode[3], opcode[2], not_6_out, opcode[0]);
  and u_lw (lw, opcode[5], not_2_out, not_3_out, not_4_out, opcode[1], opcode[0]);
  and u_sw (sw, opcode[5], not_2_out, opcode[3], not_4_out, opcode[1], opcode[0]);
  and u_beq (beq, not_1_out, not_2_out, not_3_out, opcode[2], not_6_out, not_5_out);
  and u_lui (lui, not_1_out, not_2_out, opcode[3], opcode[2], opcode[1], opcode[0]);
  and u_j (j, not_1_out, not_2_out, not_3_out, not_4_out, opcode[1], not_5_out);
  and u_lb (lb, opcode[5], not_2_out, not_3_out, not_4_out, not_6_out, not_5_out);
  and u_lh (lh, opcode[5], not_2_out, not_3_out, not_4_out, not_6_out, opcode[0]);
  and u_sb (sb, opcode[5], not_2_out, opcode[3], not_4_out, not_6_out, not_5_out);
  and u_sh (sh, opcode[5], not_2_out, opcode[3], not_4_out, not_6_out, opcode[0]);
  and u_jal (jal, not_1_out, not_2_out, not_3_out, not_4_out, opcode[1], opcode[0]);
  and u_lwor (lwor, opcode[5], not_2_out, opcode[3], opcode[2], not_6_out, opcode[0]);
  not not_7 (not_7_out, \function [5]);
  not not_8 (not_8_out, \function [4]);
  not not_9 (not_9_out, in_3);
  not not_10 (not_10_out, \function [3]);
  and and_1 (bezal_1, bezal, in_3);
  and and_2 (bezal_2, bezal, not_9_out);
  not not_11 (not_11_out, \function [2]);
  not not_12 (not_12_out, \function [1]);
  not not_13 (not_13_out, \function [0]);
  and u_add (add, \function [5], not_8_out, not_10_out, special, not_11_out, not_12_out, not_13_out);
  and u_sub (sub, \function [5], not_8_out, not_10_out, special, not_11_out, \function [1], not_13_out);
  and u_jr (jr, not_7_out, not_8_out, \function [3], special, not_11_out, not_12_out, not_13_out);
  and u_sll (sll, not_7_out, not_8_out, not_10_out, special, not_11_out, not_12_out, not_13_out);
  and u_bezal (bezal, \function [5], \function [4], not_10_out, special, not_11_out, not_12_out, \function [0]);
  and u_slo (slo, \function [5], not_8_out, \function [3], special, not_11_out, \function [1], not_13_out);
  or NPCOp1 (NPCOp[1], j, jal, bezal_1, jr);
  or NPCOp0 (NPCOp[0], beq, bezal_1, jr);
  or WRSel1 (WRSel[1], bezal_1, jal, 1'b0);
  or WRSel0 (WRSel[0], add, sub, jal, bezal_1, slo, lwor);
  or WDSel1 (WDSel[1], bezal_1, jal, 1'b0);
  or WDSel0 (WDSel[0], lw, lwor);
  or u_RFWr (RFWr, lwor, add, sub, ori, bezal_1, lui, lw, slo);
  or u_EXTOp (EXTOp, beq, sw, lw);
  or u_BSel (BSel, lui, sw, lw, ori);
  or ALUOp2 (ALUOp[2], sll, slo, lwor);
  or ALUOp1 (ALUOp[1], lwor, lui, ori, 1'b0);
  or ALUOp0 (ALUOp[0], sub, slo, beq, lui);
  or u_DMWr (DMWr, sw, lwor);
  or DMsel1 (DMsel[1], lh, sh);
  or DMsel0 (DMsel[0], lb, sb);

  // Other names for the same wires on the sheet: fun0 = \function [0]; fun1 = \function [1]; fun2 = \function [2];
  //   fun3 = \function [3]; fun4 = \function [4]; fun5 = \function [5]; op0 = opcode[0]; op1 = opcode[1];
  //   op2 = opcode[2]; op3 = opcode[3]; op4 = opcode[4]; op5 = opcode[5]
endmodule

module main (
  input  in_1,
  output [31:0] out_2,
  output out_3,
  output [4:0] out_4,
  output [31:0] out_5,
  output out_6,
  output [4:0] out_7,
  output [31:0] out_8,
  output [31:0] out_9
);

  wire alu_1_zero, clk, control_1_bsel, control_1_extop, lwor, zero2;
  wire [1:0] control_1_dmsel, control_1_npcop, control_1_wdsel, control_1_wrsel;
  wire [2:0] control_1_aluop;
  wire [4:0] multiplexer_4_out, rt, shamt, spilt_1_rd, spilt_1_rs;
  wire [5:0] \function , opcode;
  wire [15:0] spilt_1_imm16;
  wire [25:0] spilt_1_imm26;
  wire [31:0] alu_1_aluout, dm_1_out_7, ext_1_out_3, multiplexer_3_out, npc_1_npc, npc_1_pc_4, rf_1_out_8;

  Clock clock_1 (.out(clk));
  PC pc_1 (.PCin(npc_1_npc), .in_2(clk), .in_3(in_1), .PCout(out_9));
  NPC npc_1 (
    .PC(out_9), .imm26(spilt_1_imm26), .ra(rf_1_out_8), .Zero(alu_1_zero), .ALUOp(control_1_npcop),
    .PC_4(npc_1_pc_4), .NPC(npc_1_npc));
  IM im_1 (.in_1(out_9), .out_2(out_2));
  Spilt spilt_1 (
    .in_1(out_2), .opcode(opcode), .rs(spilt_1_rs), .rt(rt), .rd(spilt_1_rd), .shamt(shamt),
    .funct(\function ), .imm16(spilt_1_imm16), .imm26(spilt_1_imm26));
  Control control_1 (
    .\function (\function ), .opcode(opcode), .NPCOp(control_1_npcop), .WRSel(control_1_wrsel),
    .WDSel(control_1_wdsel), .RFWr(out_3), .EXTOp(control_1_extop), .BSel(control_1_bsel),
    .ALUOp(control_1_aluop), .DMWr(out_6), .lwor(lwor), .DMsel(control_1_dmsel), .in_3(zero2));
  Multiplexer #(.select(2), .width(5)) multiplexer_1 (
    .in0(rt), .in1(spilt_1_rd), .in2({5{1'b0}}), .in3({5{1'b1}}), .out(out_4), .sel(control_1_wrsel));  // open: en
  Multiplexer #(.select(2), .width(32)) multiplexer_2 (
    .in0({alu_1_aluout[31:7], out_7, alu_1_aluout[1:0]}), .in1(dm_1_out_7), .in2(npc_1_pc_4), .out(out_5),
    .sel(control_1_wdsel));  // open: in3, en
  EXT ext_1 (.in_1(spilt_1_imm16), .in_2(control_1_extop), .out_3(ext_1_out_3));
  RF rf_1 (
    .A1(spilt_1_rs), .A2(rt), .A3(out_4), .WD(out_5), .out_8(rf_1_out_8), .out_9(out_8), .clk(clk),
    .reset(in_1), .WE(out_3), .Zero2(zero2));
  Multiplexer #(.width(32)) multiplexer_3 (
    .in0(out_8), .in1(ext_1_out_3), .out(multiplexer_3_out), .sel(control_1_bsel));  // open: en
  Multiplexer #(.width(5)) multiplexer_4 (.in0(shamt), .in1(rt), .out(multiplexer_4_out), .sel(lwor));  // open: en
  ALU alu_1 (
    .in_1(rf_1_out_8), .in_2(multiplexer_3_out), .ALUOUT({alu_1_aluout[31:7], out_7, alu_1_aluout[1:0]}),
    .in_3(control_1_aluop), .ZERO(alu_1_zero), .shamt(multiplexer_4_out));
  DM dm_1 (
    .clk(clk), .reset(in_1), .ALU({alu_1_aluout[31:7], out_7, alu_1_aluout[1:0]}), .WD(out_8),
    .load_store(out_6), .out_7(dm_1_out_7), .DMsel(control_1_dmsel));

  // Other names for the same wires on the sheet: instr[31:0] = out_2; PC[31:0] = out_9; RegAddr[4:0] = out_4;
  //   RegData[31:0] = out_5; RegWrite = out_3; reset = in_1
endmodule

module ALU (
  input  [31:0] in_1,
  input  [31:0] in_2,
  input  [2:0] in_3,
  input  [4:0] shamt,
  output ZERO,
  output [31:0] ALUOUT
);

  wire comparator_1_eq, comparator_2_eq;
  wire [31:0] adder_1_out, adder_2_out, bit_extender_1_out, or_1_out, or_2_out, shifter_1_out, shifter_2_out,
       shifter_3_out, shifter_4_out, subtractor_1_out;

  assign bit_extender_1_out = {{27{shamt[4]}}, shamt};  // Bit_Extender bit_extender_1
  Shifter #(.width(32)) shifter_1 (.in(in_2), .\dist (5'b10000), .out(shifter_1_out));
  Shifter #(.width(32)) shifter_2 (.in(in_2), .\dist (shamt), .out(shifter_2_out));
  Shifter #(.width(32)) shifter_3 (.in(32'h1), .\dist (shamt), .out(shifter_3_out));
  Shifter #(.width(32)) shifter_4 (.in(bit_extender_1_out), .\dist (5'b00010), .out(shifter_4_out));
  Adder #(.width(32)) adder_1 (.a(in_1), .b(in_2), .out(adder_1_out));  // open: cin, cout
  Subtractor #(.width(32)) subtractor_1 (.a(in_1), .b(in_2), .out(subtractor_1_out));  // open: bin, bout
  assign or_1_out = in_1 | in_2;  // OR_Gate or_1, 32 bits wide
  Adder #(.width(32)) adder_2 (.a(adder_1_out), .b(shifter_4_out), .out(adder_2_out));  // open: cin, cout
  assign or_2_out = shifter_2_out | shifter_3_out;  // OR_Gate or_2, 32 bits wide
  Comparator #(.width(3), .mode("unsigned")) comparator_1 (.a(3'b001), .b(in_3), .eq(comparator_1_eq));  // open: gt, lt
  Comparator #(.width(32), .mode("unsigned")) comparator_2 (
    .a({32{1'b0}}), .b(subtractor_1_out), .eq(comparator_2_eq));  // open: gt, lt
  and and_1 (ZERO, comparator_1_eq, comparator_2_eq);
  Multiplexer #(.select(3), .width(32)) multiplexer_1 (
    .in0(adder_1_out), .in1(subtractor_1_out), .in2(or_1_out), .in3(shifter_1_out), .in4(shifter_2_out),
    .in5(or_2_out), .in6(adder_2_out), .out(ALUOUT), .sel(in_3));  // open: in7, en

  // Other names for the same wires on the sheet: ALUop[2:0] = in_3
endmodule

module PC (
  input  [31:0] PCin,
  input  in_2,
  input  in_3,
  output [31:0] PCout
);

  Register #(.width(32)) register_1 (.D(PCin), .Q(PCout), .clk(in_2), .clr(in_3));  // open: en

  // Other names for the same wires on the sheet: clk = in_2; reset = in_3
endmodule

module NPC (
  input  [31:0] PC,
  input  [25:0] imm26,
  input  [31:0] ra,
  input  Zero,
  input  [1:0] ALUOp,
  output [31:0] PC_4,
  output [31:0] NPC
);

  wire [31:0] bit_extender_1_out, multiplexer_1_out, PC_4_offset__0_2;

  Adder #(.width(32)) adder_1 (.a(PC), .b(32'h4), .out(PC_4));  // open: cin, cout
  assign bit_extender_1_out = {{14{imm26[15]}}, {imm26[15:0], 2'b00}};  // Bit_Extender bit_extender_1
  Adder #(.width(32)) adder_2 (.a(PC_4), .b(bit_extender_1_out), .out(PC_4_offset__0_2));  // open: cin, cout
  Multiplexer #(.width(32)) multiplexer_1 (
    .in0(PC_4), .in1(PC_4_offset__0_2), .out(multiplexer_1_out), .sel(Zero));  // open: en
  Multiplexer #(.select(2), .width(32)) multiplexer_2 (
    .in0(PC_4), .in1(multiplexer_1_out), .in2({PC[31:28], imm26, 2'b00}), .in3(ra), .out(NPC), .sel(ALUOp));  // open: en

  // Other names for the same wires on the sheet: PC31_28__instr_index__0_2[31:2] = {PC[31:28], imm26}
endmodule

module IM (
  input  [31:0] in_1,
  output [31:0] out_2
);

  wire comparator_1_gt;
  wire [31:0] multiplexer_1_out, subtractor_1_out;

  Comparator #(.width(32), .mode("unsigned")) comparator_1 (
    .a(in_1), .b(32'h3000), .gt(comparator_1_gt));  // open: eq, lt
  Subtractor #(.width(32)) subtractor_1 (.a(in_1), .b(32'h3000), .out(subtractor_1_out));  // open: bin, bout
  Multiplexer #(.width(32)) multiplexer_1 (
    .in0(in_1), .in1(subtractor_1_out), .out(multiplexer_1_out), .sel(comparator_1_gt));  // open: en
  ROM #(.addrWidth(24), .dataWidth(32)) rom_1 (.addr(multiplexer_1_out[25:2]), .data(out_2));  // open: sel

  // Notes on the sheet:
  //   contents of rom_1 (hex, n*v repeats v):
  //   5*0 868020 878820 e79020 34080000 ad040000 ad050004 ad060008 ad07000c ad100010 ad110014 ad120018
  //   8d040000 8d05000c ad04001c ad050020 34040001 34050002 34060001 10850001 10860001 ad040024 ad050028
  //   1109fffe 1000ffff
endmodule

module Spilt (
  input  [31:0] in_1,
  output [5:0] opcode,
  output [4:0] rs,
  output [4:0] rt,
  output [4:0] rd,
  output [4:0] shamt,
  output [5:0] funct,
  output [15:0] imm16,
  output [25:0] imm26
);


  assign funct = in_1[5:0];
  assign imm16 = in_1[15:0];
  assign imm26 = in_1[25:0];
  assign opcode = in_1[31:26];
  assign rd = in_1[15:11];
  assign rs = in_1[25:21];
  assign rt = in_1[20:16];
  assign shamt = in_1[10:6];
endmodule

module DM (
  input  [1:0] DMsel,
  input  clk,
  input  reset,
  input  [31:0] ALU,
  input  [31:0] WD,
  input  load_store,
  output [31:0] out_7
);

  wire decoder_1_out0, decoder_1_out1, decoder_1_out2, decoder_1_out3, decoder_2_out0, decoder_2_out1;
  wire [7:0] _0_7, _16_23, multiplexer_8_out;
  wire [15:0] multiplexer_10_out;
  wire [15:8] _0_15, _16_31;
  wire [31:0] lb, lh, multiplexer_1_out, sb, sh;

  Decoder #(.select(2)) decoder_1 (
    .out0(decoder_1_out0), .out1(decoder_1_out1), .out2(decoder_1_out2), .out3(decoder_1_out3), .sel(ALU[1:0]));  // open: en
  Decoder decoder_2 (.out0(decoder_2_out0), .out1(decoder_2_out1), .sel(ALU[1]));  // open: en
  Multiplexer #(.select(2), .width(32)) multiplexer_1 (
    .in0(WD), .in1(sh), .in2(sb), .out(multiplexer_1_out), .sel(DMsel));  // open: in3, en
  Multiplexer #(.width(8)) multiplexer_2 (.in0(_0_7), .in1(WD[7:0]), .out(sb[7:0]), .sel(decoder_1_out0));  // open: en
  Multiplexer #(.width(8)) multiplexer_3 (
    .in0(_0_15), .in1(WD[7:0]), .out(sb[15:8]), .sel(decoder_1_out1));  // open: en
  Multiplexer #(.width(8)) multiplexer_4 (
    .in0(_16_23), .in1(WD[7:0]), .out(sb[23:16]), .sel(decoder_1_out2));  // open: en
  Multiplexer #(.width(8)) multiplexer_5 (
    .in0(_16_31), .in1(WD[7:0]), .out(sb[31:24]), .sel(decoder_1_out3));  // open: en
  RAM #(.addrWidth(24), .dataWidth(32), .bus("separate")) ram_1 (
    .addr(ALU[25:2]), .din(multiplexer_1_out), .data({_16_31, _16_23, _0_15, _0_7}), .str(load_store),
    .clk(clk), .clr(reset));  // open: sel, ld
  Multiplexer #(.width(16)) multiplexer_6 (
    .in0({_0_15, _0_7}), .in1(WD[15:0]), .out(sh[15:0]), .sel(decoder_2_out0));  // open: en
  Multiplexer #(.width(16)) multiplexer_7 (
    .in0({_16_31, _16_23}), .in1(WD[15:0]), .out(sh[31:16]), .sel(decoder_2_out1));  // open: en
  Multiplexer #(.select(2), .width(8)) multiplexer_8 (
    .in0(_0_7), .in1(_0_15), .in2(_16_23), .in3(_16_31), .out(multiplexer_8_out), .sel(ALU[1:0]));  // open: en
  assign lb = {{24{multiplexer_8_out[7]}}, multiplexer_8_out};  // Bit_Extender bit_extender_1
  Multiplexer #(.select(2), .width(32)) multiplexer_9 (
    .in0({_16_31, _16_23, _0_15, _0_7}), .in1(lh), .in2(lb), .out(out_7), .sel(DMsel));  // open: in3, en
  Multiplexer #(.width(16)) multiplexer_10 (
    .in0({_0_15, _0_7}), .in1({_16_31, _16_23}), .out(multiplexer_10_out), .sel(ALU[1]));  // open: en
  assign lh = {{16{multiplexer_10_out[15]}}, multiplexer_10_out};  // Bit_Extender bit_extender_2

  // Other names for the same wires on the sheet: _0_15[7:0] = _0_7; _8_15[7:0] = _0_15; _16_31[7:0] = _16_23;
  //   _24_31[7:0] = _16_31; sel[1:0] = DMsel; byte[7:0] = WD[7:0]; half[15:0] = WD[15:0]
endmodule

module EXT (
  input  [15:0] in_1,
  input  in_2,
  output [31:0] out_3
);

  wire [31:0] bit_extender_1_out, bit_extender_2_out;

  assign bit_extender_1_out = {{16{1'b0}}, in_1};  // Bit_Extender bit_extender_1
  assign bit_extender_2_out = {{16{in_1[15]}}, in_1};  // Bit_Extender bit_extender_2
  Multiplexer #(.width(32)) multiplexer_1 (
    .in0(bit_extender_1_out), .in1(bit_extender_2_out), .out(out_3), .sel(in_2));  // open: en
endmodule

module RF (
  input  clk,
  input  reset,
  input  WE,
  input  [4:0] A1,
  input  [4:0] A2,
  input  [4:0] A3,
  input  [31:0] WD,
  output [31:0] out_8,
  output [31:0] out_9,
  output Zero2
);

  wire [31:0] _0, _1, _2, _3, _4, _5, _6, _7, _8, _9, _10, _11, _12, _13, _14, _15, _16, _17, _18, _19, _20,
       _21, _22, _23, _24, _25, _26, _27, _28, _29, _30, _31, o1, o2, o3, o4, o5, o6, o7, o8, o9, o10, o11,
       o12, o13, o14, o15, o16, o17, o18, o19, o20, o21, o22, o23, o24, o25, o26, o27, o28, o29, o30, o31;

  Demultiplexer #(.select(5), .width(32), .tristate("true")) demultiplexer_1 (
    .out1(_1), .out2(_2), .out3(_3), .out4(_4), .out5(_5), .out6(_6), .out7(_7), .out8(_8), .out9(_9),
    .out10(_10), .out11(_11), .out12(_12), .out13(_13), .out14(_14), .out15(_15), .out16(_16), .out17(_17),
    .out18(_18), .out19(_19), .out20(_20), .out21(_21), .out22(_22), .out23(_23), .out24(_24), .out25(_25),
    .out26(_26), .out27(_27), .out28(_28), .out29(_29), .out30(_30), .out31(_31), .in(WD), .sel(A3));  // open: out0, en
  Register #(.width(32)) register_1 (.D({32{1'b0}}), .en(WE), .Q(_0), .clk(clk), .clr(reset));
  Register #(.width(32)) register_2 (.D(_4), .en(WE), .Q(o4), .clk(clk), .clr(reset));
  Register #(.width(32)) register_3 (.D(_8), .en(WE), .Q(o8), .clk(clk), .clr(reset));
  Register #(.width(32)) register_4 (.D(_12), .en(WE), .Q(o12), .clk(clk), .clr(reset));
  Register #(.width(32)) register_5 (.D(_16), .en(WE), .Q(o16), .clk(clk), .clr(reset));
  Register #(.width(32)) register_6 (.D(_20), .en(WE), .Q(o20), .clk(clk), .clr(reset));
  Register #(.width(32)) register_7 (.D(_24), .en(WE), .Q(o24), .clk(clk), .clr(reset));
  Register #(.width(32)) register_8 (.D(_28), .en(WE), .Q(o28), .clk(clk), .clr(reset));
  Register #(.width(32)) register_9 (.D(_1), .en(WE), .Q(o1), .clk(clk), .clr(reset));
  Register #(.width(32)) register_10 (.D(_5), .en(WE), .Q(o5), .clk(clk), .clr(reset));
  Register #(.width(32)) register_11 (.D(_9), .en(WE), .Q(o9), .clk(clk), .clr(reset));
  Register #(.width(32)) register_12 (.D(_13), .en(WE), .Q(o13), .clk(clk), .clr(reset));
  Register #(.width(32)) register_13 (.D(_17), .en(WE), .Q(o17), .clk(clk), .clr(reset));
  Register #(.width(32)) register_14 (.D(_21), .en(WE), .Q(o21), .clk(clk), .clr(reset));
  Register #(.width(32)) register_15 (.D(_25), .en(WE), .Q(o25), .clk(clk), .clr(reset));
  Register #(.width(32)) register_16 (.D(_29), .en(WE), .Q(o29), .clk(clk), .clr(reset));
  Register #(.width(32)) register_17 (.D(_2), .en(WE), .Q(o2), .clk(clk), .clr(reset));
  Register #(.width(32)) register_18 (.D(_6), .en(WE), .Q(o6), .clk(clk), .clr(reset));
  Register #(.width(32)) register_19 (.D(_10), .en(WE), .Q(o10), .clk(clk), .clr(reset));
  Register #(.width(32)) register_20 (.D(_14), .en(WE), .Q(o14), .clk(clk), .clr(reset));
  Register #(.width(32)) register_21 (.D(_18), .en(WE), .Q(o18), .clk(clk), .clr(reset));
  Register #(.width(32)) register_22 (.D(_22), .en(WE), .Q(o22), .clk(clk), .clr(reset));
  Register #(.width(32)) register_23 (.D(_26), .en(WE), .Q(o26), .clk(clk), .clr(reset));
  Register #(.width(32)) register_24 (.D(_30), .en(WE), .Q(o30), .clk(clk), .clr(reset));
  Register #(.width(32)) register_25 (.D(_3), .en(WE), .Q(o3), .clk(clk), .clr(reset));
  Register #(.width(32)) register_26 (.D(_7), .en(WE), .Q(o7), .clk(clk), .clr(reset));
  Register #(.width(32)) register_27 (.D(_11), .en(WE), .Q(o11), .clk(clk), .clr(reset));
  Register #(.width(32)) register_28 (.D(_15), .en(WE), .Q(o15), .clk(clk), .clr(reset));
  Register #(.width(32)) register_29 (.D(_19), .en(WE), .Q(o19), .clk(clk));  // open: clr
  Register #(.width(32)) register_30 (.D(_23), .en(WE), .Q(o23), .clk(clk), .clr(reset));
  Register #(.width(32)) register_31 (.D(_27), .en(WE), .Q(o27), .clk(clk), .clr(reset));
  Register #(.width(32)) register_32 (.D(_31), .en(WE), .Q(o31), .clk(clk), .clr(reset));
  Multiplexer #(.select(5), .width(32)) multiplexer_1 (
    .in0(_0), .in1(o1), .in2(o2), .in3(o3), .in4(o4), .in5(o5), .in6(o6), .in7(o7), .in8(o8), .in9(o9),
    .in10(o10), .in11(o11), .in12(o12), .in13(o13), .in14(o14), .in15(o15), .in16(o16), .in17(o17),
    .in18(o18), .in19(o19), .in20(o20), .in21(o21), .in22(o22), .in23(o23), .in24(o24), .in25(o25),
    .in26(o26), .in27(o27), .in28(o28), .in29(o29), .in30(o30), .in31(o31), .out(out_8), .sel(A1));  // open: en
  Multiplexer #(.select(5), .width(32)) multiplexer_2 (
    .in0(_0), .in1(o1), .in2(o2), .in3(o3), .in4(o4), .in5(o5), .in6(o6), .in7(o7), .in8(o8), .in9(o9),
    .in10(o10), .in11(o11), .in12(o12), .in13(o13), .in14(o14), .in15(o15), .in16(o16), .in17(o17),
    .in18(o18), .in19(o19), .in20(o20), .in21(o21), .in22(o22), .in23(o23), .in24(o24), .in25(o25),
    .in26(o26), .in27(o27), .in28(o28), .in29(o29), .in30(o30), .in31(o31), .out(out_9), .sel(A2));  // open: en
  Comparator #(.width(32), .mode("unsigned")) comparator_1 (.a(out_9), .b({32{1'b0}}), .eq(Zero2));  // open: gt, lt
endmodule
