// Logisim project cpu.circ as structural Verilog: 11 circuits, main circuit cpu
module cpu (
);

  wire control_1_memorywrte, control_1_memtowrte, control_1_regwrite;
  wire [1:0] ALUOp, control_1_regdst, NPCOp;
  wire [4:0] multiplexer_1_out, \分线器_1_rd , \分线器_1_rs , \分线器_1_rt ;
  wire [5:0] funct, opcode;
  wire [15:0] \分线器_1_imm16 ;
  wire [25:0] \分线器_1_imm26 ;
  wire [31:0] alu_1_out_5, dm_1_out_6, ext_1_out_2, grf_1_out_8, grf_1_out_9, im_1_out_2, multiplexer_2_out,
       multiplexer_3_out, npc_1_npc, npc_1_pc_4, pc_1_pcout;

  pc pc_1 (.PCin(npc_1_npc), .PCout(pc_1_pcout));  // open: in_2, in_3
  NPC npc_1 (
    .PC(pc_1_pcout), .imm26(\分线器_1_imm26 ), .ra(grf_1_out_8), .ALUOp(NPCOp), .PC_4(npc_1_pc_4),
    .NPC(npc_1_npc));  // open: Zero
  IM im_1 (.in_1(pc_1_pcout), .out_2(im_1_out_2));
  \分线器  \u_分线器_1  (
    .in_1(im_1_out_2), .opcode(opcode), .rs(\分线器_1_rs ), .rt(\分线器_1_rt ), .rd(\分线器_1_rd ), .funct(funct),
    .imm16(\分线器_1_imm16 ), .imm26(\分线器_1_imm26 ));  // open: shamt
  Multiplexer #(.select(2), .width(5)) multiplexer_1 (
    .in0(\分线器_1_rt ), .in1(\分线器_1_rd ), .out(multiplexer_1_out), .sel(control_1_regdst));  // open: in2, in3, en
  Control control_1 (
    .in_1(opcode), .opcode(funct), .RegDst(control_1_regdst[0]), .MemtoWrte(control_1_memtowrte),
    .RegWrite(control_1_regwrite), .MemoryWrte(control_1_memorywrte), .NPCOp(NPCOp), .ALUOp(ALUOp));  // open: ALUSrc, ExtOp
  Multiplexer #(.select(2), .width(32)) multiplexer_2 (
    .in0(alu_1_out_5), .in1(dm_1_out_6), .in2(npc_1_pc_4), .out(multiplexer_2_out));  // open: in3, sel, en
  EXT ext_1 (.in_1(\分线器_1_imm16 ), .out_2(ext_1_out_2));
  grf grf_1 (
    .A1(\分线器_1_rs ), .A2(\分线器_1_rt ), .A3(multiplexer_1_out), .WD(multiplexer_2_out), .out_8(grf_1_out_8),
    .out_9(grf_1_out_9), .WE(control_1_regwrite));  // open: clk, reset
  Multiplexer #(.width(32)) multiplexer_3 (
    .in0(grf_1_out_9), .in1(ext_1_out_2), .out(multiplexer_3_out));  // open: sel, en
  ALU alu_1 (.in_1(ALUOp), .in_2(grf_1_out_8), .in_3(multiplexer_3_out), .out_5(alu_1_out_5));  // open: out_4
  DM dm_1 (
    .ALU(alu_1_out_5), .WD(grf_1_out_9), .load_store(control_1_memorywrte), .out_6(dm_1_out_6));  // open: clk, reset
  // Pins of 1 and 2 bits meet at control_1_regdst
endmodule

// RF
module grf (
  input  clk,
  input  reset,
  input  WE,
  input  [4:0] A1,
  input  [4:0] A2,
  input  [4:0] A3,
  input  [31:0] WD,
  output [31:0] out_8,
  output [31:0] out_9
);

  wire [31:0] _0, _1, _2, _3, _4, _5, _6, _7, _8, _9, _10, _11, _12, _13, _14, _15, _16, _17, _18, _19, _20,
       _21, _22, _23, _24, _25, _26, _27, _28, _29, _30, _31, o1, o2, o3, o4, o5, o6, o7, o8, o9, o10, o11,
       o12, o13, o14, o15, o16, o17, o18, o19, o20, o21, o22, o23, o24, o25, o26, o27, o28, o29, o30, o31;

  Demultiplexer #(.select(5), .width(32), .tristate("true")) demultiplexer_1 (
    .out1(_1), .out2(_2), .out3(_3), .out4(_4), .out5(_5), .out6(_6), .out7(_7), .out8(_8), .out9(_9),
    .out10(_10), .out11(_11), .out12(_12), .out13(_13), .out14(_14), .out15(_15), .out16(_16), .out17(_17),
    .out18(_18), .out19(_19), .out20(_20), .out21(_21), .out22(_22), .out23(_23), .out24(_24), .out25(_25),
    .out26(_26), .out27(_27), .out28(_28), .out29(_29), .out30(_30), .out31(_31), .in(WD), .sel(A3));  // open: out0, en
  Register #(.width(32)) register_1 (.D({32{1'b0}}), .en(WE), .Q(_0), .clk(clk), .clr(reset));
  Register #(.width(32)) register_2 (.D(_4), .en(WE), .Q(o4), .clk(clk), .clr(reset));
  Register #(.width(32)) register_3 (.D(_8), .en(WE), .Q(o8), .clk(clk), .clr(reset));
  Register #(.width(32)) register_4 (.D(_12), .en(WE), .Q(o12), .clk(clk), .clr(reset));
  Register #(.width(32)) register_5 (.D(_16), .en(WE), .Q(o16), .clk(clk), .clr(reset));
  Register #(.width(32)) register_6 (.D(_20), .en(WE), .Q(o20), .clk(clk), .clr(reset));
  Register #(.width(32)) register_7 (.D(_24), .en(WE), .Q(o24), .clk(clk), .clr(reset));
  Register #(.width(32)) register_8 (.D(_28), .en(WE), .Q(o28), .clk(clk), .clr(reset));
  Register #(.width(32)) register_9 (.D(_1), .en(WE), .Q(o1), .clk(clk), .clr(reset));
  Register #(.width(32)) register_10 (.D(_5), .en(WE), .Q(o5), .clk(clk), .clr(reset));
  Register #(.width(32)) register_11 (.D(_9), .en(WE), .Q(o9), .clk(clk), .clr(reset));
  Register #(.width(32)) register_12 (.D(_13), .en(WE), .Q(o13), .clk(clk), .clr(reset));
  Register #(.width(32)) register_13 (.D(_17), .en(WE), .Q(o17), .clk(clk), .clr(reset));
  Register #(.width(32)) register_14 (.D(_21), .en(WE), .Q(o21), .clk(clk), .clr(reset));
  Register #(.width(32)) register_15 (.D(_25), .en(WE), .Q(o25), .clk(clk), .clr(reset));
  Register #(.width(32)) register_16 (.D(_29), .en(WE), .Q(o29), .clk(clk), .clr(reset));
  Register #(.width(32)) register_17 (.D(_2), .en(WE), .Q(o2), .clk(clk), .clr(reset));
  Register #(.width(32)) register_18 (.D(_6), .en(WE), .Q(o6), .clk(clk), .clr(reset));
  Register #(.width(32)) register_19 (.D(_10), .en(WE), .Q(o10), .clk(clk), .clr(reset));
  Register #(.width(32)) register_20 (.D(_14), .en(WE), .Q(o14), .clk(clk), .clr(reset));
  Register #(.width(32)) register_21 (.D(_18), .en(WE), .Q(o18), .clk(clk), .clr(reset));
  Register #(.width(32)) register_22 (.D(_22), .en(WE), .Q(o22), .clk(clk), .clr(reset));
  Register #(.width(32)) register_23 (.D(_26), .en(WE), .Q(o26), .clk(clk), .clr(reset));
  Register #(.width(32)) register_24 (.D(_30), .en(WE), .Q(o30), .clk(clk), .clr(reset));
  Register #(.width(32)) register_25 (.D(_3), .en(WE), .Q(o3), .clk(clk), .clr(reset));
  Register #(.width(32)) register_26 (.D(_7), .en(WE), .Q(o7), .clk(clk), .clr(reset));
  Register #(.width(32)) register_27 (.D(_11), .en(WE), .Q(o11), .clk(clk), .clr(reset));
  Register #(.width(32)) register_28 (.D(_15), .en(WE), .Q(o15), .clk(clk), .clr(reset));
  Register #(.width(32)) register_29 (.D(_19), .en(WE), .Q(o19), .clk(clk));  // open: clr
  Register #(.width(32)) register_30 (.D(_23), .en(WE), .Q(o23), .clk(clk), .clr(reset));
  Register #(.width(32)) register_31 (.D(_27), .en(WE), .Q(o27), .clk(clk), .clr(reset));
  Register #(.width(32)) register_32 (.D(_31), .en(WE), .Q(o31), .clk(clk), .clr(reset));
  Multiplexer #(.select(5), .width(32)) multiplexer_1 (
    .in0(_0), .in1(o1), .in2(o2), .in3(o3), .in4(o4), .in5(o5), .in6(o6), .in7(o7), .in8(o8), .in9(o9),
    .in10(o10), .in11(o11), .in12(o12), .in13(o13), .in14(o14), .in15(o15), .in16(o16), .in17(o17),
    .in18(o18), .in19(o19), .in20(o20), .in21(o21), .in22(o22), .in23(o23), .in24(o24), .in25(o25),
    .in26(o26), .in27(o27), .in28(o28), .in29(o29), .in30(o30), .in31(o31), .out(out_8), .sel(A1));  // open: en
  Multiplexer #(.select(5), .width(32)) multiplexer_2 (
    .in0(_0), .in1(o1), .in2(o2), .in3(o3), .in4(o4), .in5(o5), .in6(o6), .in7(o7), .in8(o8), .in9(o9),
    .in10(o10), .in11(o11), .in12(o12), .in13(o13), .in14(o14), .in15(o15), .in16(o16), .in17(o17),
    .in18(o18), .in19(o19), .in20(o20), .in21(o21), .in22(o22), .in23(o23), .in24(o24), .in25(o25),
    .in26(o26), .in27(o27), .in28(o28), .in29(o29), .in30(o30), .in31(o31), .out(out_9), .sel(A2));  // open: en
endmodule

// PC
module pc (
  input  [31:0] PCin,
  input  in_2,
  input  in_3,
  output [31:0] PCout
);

  Register #(.width(32)) register_1 (.D(PCin), .Q(PCout), .clk(in_2), .clr(in_3));  // open: en

  // Other names for the same wires on the sheet: clk = in_2; reset = in_3
endmodule

module NPC (
  input  [31:0] PC,
  input  [25:0] imm26,
  input  [31:0] ra,
  input  Zero,
  input  [1:0] ALUOp,
  output [31:0] PC_4,
  output [31:0] NPC
);

  wire [31:0] bit_extender_1_out, multiplexer_1_out, PC_4_offset__0_2;

  Adder #(.width(32)) adder_1 (.a(PC), .b(32'h4), .out(PC_4));  // open: cin, cout
  assign bit_extender_1_out = {{14{imm26[15]}}, {imm26[15:0], 2'b00}};  // Bit_Extender bit_extender_1
  Adder #(.width(32)) adder_2 (.a(PC_4), .b(bit_extender_1_out), .out(PC_4_offset__0_2));  // open: cin, cout
  Multiplexer #(.width(32)) multiplexer_1 (
    .in0(PC_4), .in1(PC_4_offset__0_2), .out(multiplexer_1_out), .sel(Zero));  // open: en
  Multiplexer #(.select(2), .width(32)) multiplexer_2 (
    .in0(PC_4), .in1(multiplexer_1_out), .in2({PC[31:28], imm26, 2'b00}), .in3(ra), .out(NPC), .sel(ALUOp));  // open: en

  // Other names for the same wires on the sheet: PC31_28__instr_index__0_2[31:2] = {PC[31:28], imm26}
endmodule

module IM (
  input  [31:0] in_1,
  output [31:0] out_2
);

  ROM #(.addrWidth(5), .dataWidth(32)) rom_1 (.addr(in_1[6:2]), .data(out_2));  // open: sel
endmodule

module ALU (
  input  [1:0] in_1,
  input  [31:0] in_2,
  input  [31:0] in_3,
  output out_4,
  output [31:0] out_5
);

  wire [31:0] adder_1_out, multiplexer_1_out, not_1_out, or_1_out;

  assign not_1_out = ~in_3;  // NOT_Gate not_1, 32 bits wide
  Multiplexer #(.width(32)) multiplexer_1 (
    .in0(in_3), .in1(not_1_out), .out(multiplexer_1_out), .sel(in_1[0]));  // open: en
  Adder #(.width(32)) adder_1 (.a(in_2), .b(multiplexer_1_out), .out(adder_1_out), .cin(in_1[0]));  // open: cout
  assign or_1_out = in_3 | in_2;  // OR_Gate or_1, 32 bits wide
  Comparator #(.width(32)) comparator_1 (.a({32{1'b0}}), .b(adder_1_out), .eq(out_4));  // open: gt, lt
  Multiplexer #(.width(32)) multiplexer_2 (.in0(adder_1_out), .in1(or_1_out), .out(out_5), .sel(in_1[1]));  // open: en

  // Other names for the same wires on the sheet: sel1 = in_1[0]; sel2 = in_1[1]
endmodule

// Spilt
module \分线器  (
  input  [31:0] in_1,
  output [5:0] opcode,
  output [4:0] rs,
  output [4:0] rt,
  output [4:0] rd,
  output [4:0] shamt,
  output [5:0] funct,
  output [15:0] imm16,
  output [25:0] imm26
);


  assign funct = in_1[5:0];
  assign imm16 = in_1[15:0];
  assign imm26 = in_1[25:0];
  assign opcode = in_1[31:26];
  assign rd = in_1[15:11];
  assign rs = in_1[25:21];
  assign rt = in_1[20:16];
  assign shamt = in_1[10:6];
endmodule

module DM (
  input  clk,
  input  reset,
  input  [31:0] ALU,
  input  [31:0] WD,
  input  load_store,
  output [31:0] out_6
);

  wire not_1_out;

  RAM #(.dataWidth(32), .bus("separate")) ram_1 (
    .addr(ALU[9:2]), .din(WD), .data(out_6), .str(load_store), .clk(clk), .ld(not_1_out), .clr(reset));  // open: sel
  not not_1 (not_1_out, load_store);
endmodule

module EXT (
  input  [15:0] in_1,
  output [31:0] out_2
);

  assign out_2 = {{16{in_1[15]}}, in_1};  // Bit_Extender bit_extender_1
endmodule

module Control (
  input  [5:0] in_1,
  input  [5:0] opcode,
  output MemtoWrte,
  output MemoryWrte,
  output [1:0] ALUOp,
  output RegDst,
  output ALUSrc,
  output RegWrite,
  output ExtOp,
  output [1:0] NPCOp
);

  wire add, add_2_out, and_1_out, and_2_out, and_3_out, b_jump, beq, j, j_jump, jr, jr_jump, lui, not_1_out,
       not_2_out, not_3_out, not_4_out, not_5_out, not_6_out, not_8_out, not_9_out, not_11_out, not_13_out,
       not_14_out, not_15_out, not_16_out, not_17_out, ori, special, sub, sub_2_out;

  not not_1 (not_1_out, opcode[5]);
  not not_2 (not_2_out, opcode[4]);
  not not_3 (not_3_out, opcode[3]);
  not not_4 (not_4_out, opcode[2]);
  not not_5 (not_5_out, opcode[1]);
  not not_6 (not_6_out, opcode[0]);
  and u_special (special, not_1_out, not_2_out, not_3_out, not_4_out, not_5_out, not_6_out);
  and u_ori (ori, not_1_out, not_2_out, opcode[3], opcode[2], not_5_out, opcode[0]);
  and lw (MemtoWrte, opcode[5], not_2_out, not_3_out, not_4_out, opcode[1], opcode[0]);
  and sw (MemoryWrte, opcode[5], not_2_out, opcode[3], not_4_out, opcode[1], opcode[0]);
  and u_beq (beq, not_1_out, not_2_out, not_3_out, opcode[2], not_5_out, not_6_out);
  and u_lui (lui, not_1_out, not_2_out, opcode[3], opcode[2], opcode[1]);
  and u_j (j, not_1_out, not_2_out, not_3_out, not_4_out, opcode[1], not_6_out);
  and and_1 (and_1_out, special, add);
  and and_2 (and_2_out, special, sub);
  and and_3 (and_3_out, special, jr);
  or u_RegDst (RegDst, and_1_out, and_2_out);
  or u_ALUSrc (ALUSrc, ori, MemtoWrte, MemoryWrte);
  // NOT_Gate not_7 has open pins: in=b_jump, out=open
  not not_8 (not_8_out, in_1[4]);
  not not_9 (not_9_out, in_1[5]);
  // NOT_Gate not_10 has open pins: in=jr_jump, out=open
  not not_11 (not_11_out, in_1[3]);
  or u_RegWrite (RegWrite, and_1_out, and_2_out, ori, MemtoWrte);
  // NOT_Gate not_12 has open pins: in=j_jump, out=open
  not not_13 (not_13_out, in_1[2]);
  not not_14 (not_14_out, in_1[0]);
  not not_15 (not_15_out, in_1[1]);
  buf or_1 (b_jump, beq);  // OR_Gate
  or or_2 (NPCOp[1], jr_jump, j_jump);
  or or_3 (NPCOp[0], jr_jump, b_jump);
  buf or_4 (jr_jump, and_3_out);  // OR_Gate
  and u_add (add, in_1[5], not_8_out, not_11_out, not_13_out, not_15_out, not_14_out);
  and u_sub (sub, in_1[5], not_8_out, not_11_out, not_13_out, in_1[1], not_14_out);
  and u_jr (jr, not_9_out, not_8_out, in_1[3], not_13_out, not_15_out, not_14_out);
  or u_ExtOp (ExtOp, MemtoWrte, MemoryWrte);
  buf or_5 (j_jump, j);  // OR_Gate
  or add_2 (add_2_out, and_1_out, MemtoWrte, MemoryWrte);
  not not_16 (not_16_out, ori);
  not not_17 (not_17_out, add_2_out);
  or sub_2 (sub_2_out, and_2_out, beq);
  // NOT_Gate not_18 has open pins: in=sub_2_out, out=open
  xnor xnor_1 (ALUOp[1], add_2_out, sub_2_out);
  or or_6 (ALUOp[0], not_16_out, not_17_out);

  // Other names for the same wires on the sheet: fun0 = in_1[0]; fun1 = in_1[1]; fun2 = in_1[2]; fun3 = in_1[3];
  //   fun4 = in_1[4]; fun5 = in_1[5]; lw = MemtoWrte; op0 = opcode[0]; op1 = opcode[1]; op2 = opcode[2];
  //   op3 = opcode[3]; op4 = opcode[4]; op5 = opcode[5]; sw = MemoryWrte
endmodule

module a (
  input  a,
  input  b,
  input  c,
  output x,
  output y
);

  or or_1 (x, c, a);
  or or_2 (y, b, a);
endmodule
