// Logisim project fabonacci.circ as structural Verilog: 3 circuits, main circuit 计数逻辑
module \计数逻辑  (
  input  [2:0] in_1,
  output enable,
  output out_3
);

  wire and_1_out, clock_1_out, comparator_1_eq, not_1_out;
  wire [3:0] adder_1_out, bit_extender_1_out, counter_1_q;

  not not_1 (not_1_out, comparator_1_eq);
  and and_1 (and_1_out, not_1_out, out_3);
  assign bit_extender_1_out = {{1{1'b0}}, in_1};  // Bit_Extender bit_extender_1
  Counter #(.width(4), .max('hf)) counter_1 (
    .count(and_1_out), .Q(counter_1_q), .clk(clock_1_out));  // open: load, D, carry, clr
  Clock clock_1 (.out(clock_1_out));
  Adder #(.width(4)) adder_1 (.a(bit_extender_1_out), .b(4'b0001), .out(adder_1_out));  // open: cin, cout
  Comparator #(.width(4), .mode("unsigned")) comparator_1 (
    .a(4'b0000), .b(adder_1_out), .eq(comparator_1_eq));  // open: gt, lt
  Comparator #(.width(4), .mode("unsigned")) comparator_2 (
    .a(adder_1_out), .b(counter_1_q), .gt(out_3));  // open: eq, lt
  not not_2 (enable, comparator_1_eq);
endmodule

module \计算逻辑  (
  input  in_1,
  input  in_2,
  output [3:0] out_3
);

  wire clock_1_out, clock_2_out, clock_3_out, Flag, if1;
  wire [3:0] adder_1_out, counter_1_q, multiplexer_1_out, multiplexer_2_out, now, pre;

  and and_1 (Flag, in_2, in_1);
  Clock clock_1 (.out(clock_1_out));
  Multiplexer #(.width(4)) multiplexer_1 (.in0(now), .in1(4'b0000), .out(multiplexer_1_out), .sel(if1));  // open: en
  Counter #(.width(4), .max('hf)) counter_1 (
    .count(in_2), .Q(counter_1_q), .clk(clock_1_out));  // open: load, D, carry, clr
  Multiplexer #(.width(4)) multiplexer_2 (.in0(now), .in1(4'b0001), .out(multiplexer_2_out), .sel(if1));  // open: en
  Adder #(.width(4)) adder_1 (.a(pre), .b(multiplexer_1_out), .out(adder_1_out));  // open: cin, cout
  Comparator #(.width(4), .mode("unsigned")) comparator_1 (.a(counter_1_q), .b(4'b0001), .lt(if1));  // open: gt, eq
  // Probe on multiplexer_2_out
  Clock clock_2 (.out(clock_2_out));
  Register #(.width(4)) register_1 (.D(adder_1_out), .en(Flag), .Q(now), .clk(clock_3_out));  // open: clr
  Clock clock_3 (.out(clock_3_out));
  Register #(.width(4)) register_2 (.D(multiplexer_2_out), .en(Flag), .Q(pre), .clk(clock_2_out));  // open: clr
  Multiplexer #(.width(4)) multiplexer_3 (.in0(now), .in1(4'b0000), .out(out_3), .sel(in_2));  // open: en

  // Other names for the same wires on the sheet: enable = in_1; flag_t = in_2
endmodule

module main (
  input  [2:0] in_1,
  output [3:0] out_2
);

  wire \计数逻辑_1_enable , \计数逻辑_1_out_3 ;

  \计数逻辑  \u_计数逻辑_1  (.in_1(in_1), .enable(\计数逻辑_1_enable ), .out_3(\计数逻辑_1_out_3 ));
  \计算逻辑  \u_计算逻辑_1  (.in_1(\计数逻辑_1_enable ), .in_2(\计数逻辑_1_out_3 ), .out_3(out_2));
endmodule
