// Logisim project fei.circ as structural Verilog
module select (
  input  [3:0] in_1,
  output [3:0] out_2
);

  wire flag;

  Comparator #(.width(4), .mode("unsigned")) comparator_1 (.a(in_1), .b(4'b0000), .eq(flag));  // open: gt, lt
  swap swap_1 (.a(in_1[2]), .b(1'b0), .c(flag), .x(out_2[2]));  // open: y
  swap swap_2 (.a(in_1[3]), .b(1'b0), .c(flag), .x(out_2[3]));  // open: y
  swap swap_3 (.a(in_1[0]), .b(1'b1), .c(flag), .x(out_2[0]));  // open: y
  swap swap_4 (.a(in_1[1]), .b(1'b0), .c(flag), .x(out_2[1]));  // open: y

  // Other names for the same wires on the sheet: i0 = in_1[0]; i1 = in_1[1]; i2 = in_1[2]; i3 = in_1[3];
  //   o0 = out_2[0]; o1 = out_2[1]; o2 = out_2[2]; o3 = out_2[3]
endmodule

module swap (
  input  a,
  input  b,
  input  c,
  output x,
  output y
);

  wire and_1_out, and_2_out, and_3_out, and_4_out, not_1_out, not_2_out;

  not not_1 (not_1_out, c);
  not not_2 (not_2_out, c);
  and and_1 (and_1_out, b, c);
  and and_2 (and_2_out, a, not_1_out);
  and and_3 (and_3_out, b, not_2_out);
  and and_4 (and_4_out, a, c);
  or or_1 (x, and_1_out, and_2_out);
  or or_2 (y, and_3_out, and_4_out);
endmodule

module tip (
);

  wire clock_1_out;
  wire [2:0] register_1_q, undriven;

  Clock clock_1 (.out(clock_1_out));
  Register #(.width(3)) register_1 (.D(undriven), .Q(register_1_q), .clk(clock_1_out), .clr(1'b1));  // open: en
endmodule
