// Logisim project fsm.circ as structural Verilog: 3 circuits, main circuit fsm
module fsm (
  input  in_1,
  input  [1:0] in_2,
  output out_3
);

  wire clock_1_out;
  wire [2:0] register_1_q, \状态转移_1_out_4 ;

  \状态转移  \u_状态转移_1  (.in_1(register_1_q), .in_2(in_2), .in_3(in_1), .out_4(\状态转移_1_out_4 ));
  Register #(.width(3)) register_1 (.D(\状态转移_1_out_4 ), .Q(register_1_q), .clk(clock_1_out));  // open: en, clr
  Clock clock_1 (.out(clock_1_out));
  // Probe on register_1_q
  \输出结果  \u_输出结果_1  (.in_1(register_1_q), .in_2(in_2), .out_3(out_3));

  // Other names for the same wires on the sheet: clr = in_1
endmodule

module \状态转移  (
  input  [2:0] in_1,
  input  [1:0] in_2,
  input  in_3,
  output [2:0] out_4
);

  wire and_2_out, and_3_out, and_4_out, and_5_out, and_6_out, and_7_out, and_8_out, and_9_out, c0, c1, c2,
       not_1_out, not_2_out, not_3_out, not_4_out, not_5_out, not_6_out, not_7_out, not_8_out, not_9_out,
       not_10_out, not_11_out, not_12_out, not_13_out, not_14_out, not_15_out, not_16_out, not_17_out,
       not_18_out, not_19_out, not_20_out, not_21_out, not_22_out, not_23_out, not_24_out, not_25_out;

  not not_1 (not_1_out, in_1[2]);
  not not_2 (not_2_out, in_2[0]);
  not not_3 (not_3_out, in_1[2]);
  not not_4 (not_4_out, in_1[1]);
  not not_5 (not_5_out, in_2[1]);
  not not_6 (not_6_out, in_1[2]);
  not not_7 (not_7_out, in_1[1]);
  not not_8 (not_8_out, in_2[0]);
  not not_9 (not_9_out, in_1[2]);
  not not_10 (not_10_out, in_1[0]);
  not not_11 (not_11_out, in_2[1]);
  not not_12 (not_12_out, in_1[2]);
  not not_13 (not_13_out, in_1[0]);
  not not_14 (not_14_out, in_2[0]);
  not not_15 (not_15_out, in_1[1]);
  not not_16 (not_16_out, in_1[0]);
  not not_17 (not_17_out, in_2[1]);
  not not_18 (not_18_out, in_1[2]);
  not not_19 (not_19_out, in_1[1]);
  not not_20 (not_20_out, in_2[0]);
  not not_21 (not_21_out, in_1[2]);
  not not_22 (not_22_out, in_1[0]);
  not not_23 (not_23_out, in_2[0]);
  not not_24 (not_24_out, in_1[2]);
  not not_25 (not_25_out, in_2[1]);
  and and_1 (c2, not_1_out, in_1[1], in_1[0], not_2_out);
  and and_2 (and_2_out, not_3_out, not_4_out, in_1[0], not_5_out);
  and and_3 (and_3_out, not_6_out, not_7_out, in_1[0], not_8_out);
  and and_4 (and_4_out, not_9_out, in_1[1], not_10_out, not_11_out);
  and and_5 (and_5_out, not_12_out, in_1[1], not_13_out, not_14_out);
  and and_6 (and_6_out, not_15_out, not_16_out, not_17_out, in_2[0]);
  and and_7 (and_7_out, not_18_out, not_19_out, in_1[0], not_20_out);
  and and_8 (and_8_out, not_21_out, in_1[1], not_22_out, not_23_out);
  and and_9 (and_9_out, not_24_out, in_1[1], in_1[0], not_25_out, in_2[0]);
  or or_1 (c1, and_2_out, and_3_out, and_4_out, and_5_out);
  or or_2 (c0, and_6_out, and_7_out, and_8_out, and_9_out);
  Multiplexer #(.width(3)) multiplexer_1 (.in0({c2, c1, c0}), .in1(3'b000), .out(out_4), .sel(in_3));  // open: en

  // Other names for the same wires on the sheet: clr = in_3; a0 = in_1[0]; a1 = in_1[1]; a2 = in_1[2]; b0 = in_2[0];
  //   b1 = in_2[1]
endmodule

module \输出结果  (
  input  [2:0] in_1,
  input  [1:0] in_2,
  output out_3
);

  wire comparator_1_eq, comparator_2_eq, comparator_3_eq, or_1_out;

  Comparator #(.width(3), .mode("unsigned")) comparator_1 (.a(in_1), .b(3'b011), .eq(comparator_1_eq));  // open: gt, lt
  Comparator #(.width(2), .mode("unsigned")) comparator_2 (.a(2'b10), .b(in_2), .eq(comparator_2_eq));  // open: gt, lt
  Comparator #(.width(2), .mode("unsigned")) comparator_3 (.a(in_2), .b(2'b00), .eq(comparator_3_eq));  // open: gt, lt
  or or_1 (or_1_out, comparator_2_eq, comparator_3_eq);
  and and_1 (out_3, comparator_1_eq, or_1_out);
endmodule
