// Logisim project ftoi.circ as structural Verilog: 6 circuits, main circuit ftoi
module ftoi (
  input  [15:0] in_1,
  output [31:0] out_2
);

  wire judhe_1_out_2, \是否_1_1_out_2 , \输出0_1_out_2 ;
  wire [4:0] \幂次_1_out_2 ;
  wire [16:0] sll_1_out_5;
  wire [31:0] adder_1_out, bit_extender_1_out, multiplexer_1_out, not_1_out;

  \是否_1  \u_是否_1_1  (.in_1(in_1[14:10]), .out_2(\是否_1_1_out_2 ));
  judhe judhe_1 (.in_1(in_1[14:10]), .out_2(judhe_1_out_2));
  \幂次  \u_幂次_1  (.in_1(in_1[14:10]), .out_2(\幂次_1_out_2 ));
  \输出0  \u_输出0_1  (.in_1(in_1[14:10]), .out_2(\输出0_1_out_2 ));
  sll sll_1 (
    .in_1(in_1[9:0]), .in_2(\是否_1_1_out_2 ), .\幂是否小于0 (judhe_1_out_2), .in_4(\幂次_1_out_2 ),
    .out_5(sll_1_out_5));
  assign bit_extender_1_out = {{15{1'b0}}, sll_1_out_5};  // Bit_Extender bit_extender_1
  assign not_1_out = ~bit_extender_1_out;  // NOT_Gate not_1, 32 bits wide
  Adder #(.width(32)) adder_1 (.a(not_1_out), .b(32'h1), .out(adder_1_out));  // open: cin, cout
  Multiplexer #(.width(32)) multiplexer_1 (
    .in0(bit_extender_1_out), .in1(adder_1_out), .out(multiplexer_1_out), .sel(in_1[15]));  // open: en
  Multiplexer #(.width(32)) multiplexer_2 (
    .in0(multiplexer_1_out), .in1({32{1'b0}}), .out(out_2), .sel(\输出0_1_out_2 ));  // open: en

  // Other names for the same wires on the sheet: 幂次[4:0] = in_1[14:10]; tunnel = in_1[15]
endmodule

module judhe (
  input  [4:0] in_1,
  output out_2
);

  wire [3:0] subtractor_1_out;

  Subtractor #(.width(5)) subtractor_1 (.a(in_1), .b(5'b01111), .out({out_2, subtractor_1_out}));  // open: bin, bout
  // Probe on {out_2, subtractor_1_out}
endmodule

module sll (
  input  [9:0] in_1,
  input  in_2,
  input  \幂是否小于0 ,
  input  [4:0] in_4,
  output [16:0] out_5
);

  wire subtractor_1_bout;
  wire [4:0] subtractor_1_out, subtractor_2_out;
  wire [10:0] flag1;
  wire [16:0] bit_extender_1_out, bit_extender_2_out, multiplexer_2_out, multiplexer_3_out, shifter_1_out,
       shifter_2_out;

  Subtractor #(.width(5)) subtractor_1 (
    .a(5'b01010), .b(in_4), .out(subtractor_1_out), .bout(subtractor_1_bout));  // open: bin
  // Probe on subtractor_1_out
  Multiplexer #(.width(11)) multiplexer_1 (
    .in0({in_2, in_1}), .in1({11{1'b0}}), .out(flag1), .sel(\幂是否小于0 ));  // open: en
  assign bit_extender_1_out = {{6{1'b0}}, flag1};  // Bit_Extender bit_extender_1
  assign bit_extender_2_out = {{6{1'b0}}, flag1};  // Bit_Extender bit_extender_2
  Subtractor #(.width(5)) subtractor_2 (.a(in_4), .b(5'b01010), .out(subtractor_2_out));  // open: bin, bout
  // Probe on bit_extender_1_out
  Shifter #(.width(17), .shift("lr")) shifter_1 (
    .in(bit_extender_1_out), .\dist (subtractor_1_out), .out(shifter_1_out));
  Shifter #(.width(17)) shifter_2 (.in(bit_extender_2_out), .\dist (subtractor_2_out), .out(shifter_2_out));
  Multiplexer #(.width(17)) multiplexer_2 (
    .in0(shifter_1_out), .in1({17{1'b0}}), .out(multiplexer_2_out), .sel(\幂是否小于0 ));  // open: en
  Multiplexer #(.width(17)) multiplexer_3 (
    .in0(shifter_2_out), .in1({17{1'b0}}), .out(multiplexer_3_out), .sel(\幂是否小于0 ));  // open: en
  Multiplexer #(.width(17)) multiplexer_4 (
    .in0(multiplexer_2_out), .in1(multiplexer_3_out), .out(out_5), .sel(subtractor_1_bout));  // open: en

  // Other names for the same wires on the sheet: flag0[10:0] = {in_2, in_1}
endmodule

module \幂次  (
  input  [4:0] in_1,
  output [4:0] out_2
);

  Subtractor #(.width(5)) subtractor_1 (.a(in_1), .b(5'b01111), .out(out_2));  // open: bin, bout
endmodule

module \是否_1  (
  input  [4:0] in_1,
  output out_2
);

  wire comparator_1_eq, comparator_2_eq;

  Comparator #(.width(5), .mode("unsigned")) comparator_1 (
    .a(in_1), .b({5{1'b1}}), .eq(comparator_1_eq));  // open: gt, lt
  Comparator #(.width(5), .mode("unsigned")) comparator_2 (
    .a(in_1), .b({5{1'b0}}), .eq(comparator_2_eq));  // open: gt, lt
  nor nor_1 (out_2, comparator_2_eq, comparator_1_eq);
endmodule

module \输出0  (
  input  [4:0] in_1,
  output out_2
);

  Comparator #(.width(5), .mode("unsigned")) comparator_1 (.a(in_1), .b({5{1'b1}}), .eq(out_2));  // open: gt, lt
endmodule
