// Logisim project 斐波那契2.circ as structural Verilog: 8 circuits, main circuit main
module main (
  input  [31:0] in_1,
  output [31:0] out_2
);

  wire freeze, n_low;

  \技术逻辑  \u_技术逻辑_1  (.in_1(in_1), .in_2(1'b0), .n_low(n_low), .freeze(freeze));
  \计算逻辑  \u_计算逻辑_1  (.in_1(n_low), .in_2(freeze), .in_3(1'b0), .out_4(out_2));

  // Other names for the same wires on the sheet: input[31:0] = in_1
endmodule

module \寄存器矩阵  (
  input  [31:0] a11_in,
  input  [31:0] a12_in,
  input  [31:0] a21_in,
  input  [31:0] a22_in,
  input  in_5,
  input  in_6,
  input  in_7,
  output [31:0] out_8,
  output [31:0] out_9,
  output [31:0] out_10,
  output [31:0] out_11
);

  Register #(.width(32)) register_1 (.D(a11_in), .en(in_5), .Q(out_8), .clk(in_6), .clr(in_7));
  Register #(.width(32)) register_2 (.D(a12_in), .en(in_5), .Q(out_9), .clk(in_6), .clr(in_7));
  Register #(.width(32)) register_3 (.D(a21_in), .en(in_5), .Q(out_10), .clk(in_6), .clr(in_7));
  Register #(.width(32)) register_4 (.D(a22_in), .en(in_5), .Q(out_11), .clk(in_6), .clr(in_7));

  // Other names for the same wires on the sheet: a11_out[31:0] = out_8; a12_out[31:0] = out_9; a21_out[31:0] = out_10;
  //   a22_out[31:0] = out_11; clk = in_6; clr = in_7; ena = in_5
endmodule

module \矩阵MUX  (
  input  [31:0] in_1,
  input  [31:0] in_2,
  input  [31:0] in_3,
  input  [31:0] in_4,
  input  [31:0] in_5,
  input  [31:0] in_6,
  input  [31:0] in_7,
  input  [31:0] in_8,
  input  in_9,
  output [31:0] out_10,
  output [31:0] out_11,
  output [31:0] out_12,
  output [31:0] out_13
);

  Multiplexer #(.width(32)) multiplexer_1 (.in0(in_1), .in1(in_5), .out(out_10), .sel(in_9));  // open: en
  Multiplexer #(.width(32)) multiplexer_2 (.in0(in_2), .in1(in_6), .out(out_11), .sel(in_9));  // open: en
  Multiplexer #(.width(32)) multiplexer_3 (.in0(in_3), .in1(in_7), .out(out_12), .sel(in_9));  // open: en
  Multiplexer #(.width(32)) multiplexer_4 (.in0(in_4), .in1(in_8), .out(out_13), .sel(in_9));  // open: en

  // Other names for the same wires on the sheet: a11[31:0] = in_1; a12[31:0] = in_2; a21[31:0] = in_3;
  //   a22[31:0] = in_4; b11[31:0] = in_5; b12[31:0] = in_6; b21[31:0] = in_7; b22[31:0] = in_8; out11[31:0] = out_10;
  //   out12[31:0] = out_11; out21[31:0] = out_12; out22[31:0] = out_13; select = in_9
endmodule

module \矩阵初始值  (
  output [31:0] out_1,
  output [31:0] out_2,
  output [31:0] out_3,
  output [31:0] out_4
);


  assign out_1 = 32'h1;
  assign out_2 = 32'h1;
  assign out_3 = 32'h1;
  assign out_4 = {32{1'b0}};
endmodule

module \单位阵  (
  output [31:0] out_1,
  output [31:0] out_2,
  output [31:0] out_3,
  output [31:0] out_4
);


  assign out_1 = 32'h1;
  assign out_2 = {32{1'b0}};
  assign out_3 = 32'h1;
  assign out_4 = {32{1'b0}};
endmodule

module \计算逻辑  (
  input  in_1,
  input  in_2,
  input  in_3,
  output [31:0] out_4
);

  wire clk, ena, init;
  wire [31:0] a11, a12, a21, a22, s11, s12, s21, s22, \单位阵_1_out_1 , \单位阵_1_out_2 , \单位阵_1_out_3 ,
       \单位阵_1_out_4 , \单位阵_2_out_1 , \单位阵_2_out_2 , \单位阵_2_out_3 , \单位阵_2_out_4 , \矩阵mux_1_out_10 ,
       \矩阵mux_1_out_11 , \矩阵mux_1_out_12 , \矩阵mux_1_out_13 , \矩阵mux_2_out_10 , \矩阵mux_2_out_11 ,
       \矩阵mux_2_out_12 , \矩阵mux_2_out_13 , \矩阵mux_3_out_10 , \矩阵mux_3_out_11 , \矩阵mux_3_out_12 ,
       \矩阵mux_3_out_13 , \矩阵初始值_1_out_1 , \矩阵初始值_1_out_2 , \矩阵初始值_1_out_3 , \矩阵初始值_1_out_4 , \矩阵计算器_1_out_9 ,
       \矩阵计算器_1_out_10 , \矩阵计算器_1_out_11 , \矩阵计算器_1_out_12 , \矩阵计算器_2_out_9 , \矩阵计算器_2_out_10 ,
       \矩阵计算器_2_out_11 , \矩阵计算器_2_out_12 ;

  Counter #(.width(1), .max('h1)) counter_1 (.Q(init), .clk(clk), .clr(in_3));  // open: load, D, count, carry
  Clock clock_1 (.out(clk));
  not not_1 (ena, in_2);
  \单位阵  \u_单位阵_1  (.out_1(\单位阵_1_out_1 ), .out_2(\单位阵_1_out_2 ), .out_3(\单位阵_1_out_3 ), .out_4(\单位阵_1_out_4 ));
  \矩阵MUX  \u_矩阵mux_1  (
    .in_1(\单位阵_1_out_1 ), .in_2(\单位阵_1_out_2 ), .in_3(\单位阵_1_out_3 ), .in_4(\单位阵_1_out_4 ), .in_5(a11),
    .in_6(a12), .in_7(a21), .in_8(a22), .in_9(in_1), .out_10(\矩阵mux_1_out_10 ), .out_11(\矩阵mux_1_out_11 ),
    .out_12(\矩阵mux_1_out_12 ), .out_13(\矩阵mux_1_out_13 ));
  Multiplexer #(.width(32)) multiplexer_1 (.in0({32{1'b0}}), .in1(s12), .out(out_4), .sel(in_2));  // open: en
  \矩阵计算器  \u_矩阵计算器_1  (
    .in_1(a11), .in_2(a12), .in_3(a21), .in_4(a22), .in_5(a11), .in_6(a12), .in_7(a21), .in_8(a22),
    .out_9(\矩阵计算器_1_out_9 ), .out_10(\矩阵计算器_1_out_10 ), .out_11(\矩阵计算器_1_out_11 ), .out_12(\矩阵计算器_1_out_12 ));
  \矩阵计算器  \u_矩阵计算器_2  (
    .in_1(s11), .in_2(s12), .in_3(s21), .in_4(s22), .in_5(\矩阵mux_1_out_10 ), .in_6(\矩阵mux_1_out_11 ),
    .in_7(\矩阵mux_1_out_12 ), .in_8(\矩阵mux_1_out_13 ), .out_9(\矩阵计算器_2_out_9 ), .out_10(\矩阵计算器_2_out_10 ),
    .out_11(\矩阵计算器_2_out_11 ), .out_12(\矩阵计算器_2_out_12 ));
  \矩阵初始值  \u_矩阵初始值_1  (
    .out_1(\矩阵初始值_1_out_1 ), .out_2(\矩阵初始值_1_out_2 ), .out_3(\矩阵初始值_1_out_3 ), .out_4(\矩阵初始值_1_out_4 ));
  \单位阵  \u_单位阵_2  (.out_1(\单位阵_2_out_1 ), .out_2(\单位阵_2_out_2 ), .out_3(\单位阵_2_out_3 ), .out_4(\单位阵_2_out_4 ));
  \矩阵MUX  \u_矩阵mux_2  (
    .in_1(\矩阵初始值_1_out_1 ), .in_2(\矩阵初始值_1_out_2 ), .in_3(\矩阵初始值_1_out_3 ), .in_4(\矩阵初始值_1_out_4 ),
    .in_5(\矩阵计算器_1_out_9 ), .in_6(\矩阵计算器_1_out_10 ), .in_7(\矩阵计算器_1_out_11 ), .in_8(\矩阵计算器_1_out_12 ),
    .in_9(init), .out_10(\矩阵mux_2_out_10 ), .out_11(\矩阵mux_2_out_11 ), .out_12(\矩阵mux_2_out_12 ),
    .out_13(\矩阵mux_2_out_13 ));
  \矩阵MUX  \u_矩阵mux_3  (
    .in_1(\单位阵_2_out_1 ), .in_2(\单位阵_2_out_2 ), .in_3(\单位阵_2_out_3 ), .in_4(\单位阵_2_out_4 ),
    .in_5(\矩阵计算器_2_out_9 ), .in_6(\矩阵计算器_2_out_10 ), .in_7(\矩阵计算器_2_out_11 ), .in_8(\矩阵计算器_2_out_12 ),
    .out_10(\矩阵mux_3_out_10 ), .out_11(\矩阵mux_3_out_11 ), .out_12(\矩阵mux_3_out_12 ), .out_13(\矩阵mux_3_out_13 ));  // open: in_9
  \寄存器矩阵  \u_寄存器矩阵_1  (
    .a11_in(\矩阵mux_3_out_10 ), .a12_in(\矩阵mux_3_out_11 ), .a21_in(\矩阵mux_3_out_12 ),
    .a22_in(\矩阵mux_3_out_13 ), .in_5(ena), .in_6(clk), .in_7(in_3), .out_8(s11), .out_9(s12), .out_10(s21),
    .out_11(s22));
  \寄存器矩阵  \u_寄存器矩阵_2  (
    .a11_in(\矩阵mux_2_out_10 ), .a12_in(\矩阵mux_2_out_11 ), .a21_in(\矩阵mux_2_out_12 ),
    .a22_in(\矩阵mux_2_out_13 ), .in_5(ena), .in_6(clk), .in_7(in_3), .out_8(a11), .out_9(a12), .out_10(a21),
    .out_11(a22));

  // Other names for the same wires on the sheet: clr = in_3; freeze = in_2; n_low = in_1
endmodule

module \矩阵计算器  (
  input  [31:0] in_1,
  input  [31:0] in_2,
  input  [31:0] in_3,
  input  [31:0] in_4,
  input  [31:0] in_5,
  input  [31:0] in_6,
  input  [31:0] in_7,
  input  [31:0] in_8,
  output [31:0] out_9,
  output [31:0] out_10,
  output [31:0] out_11,
  output [31:0] out_12
);

  wire [31:0] multiplier_1_out, multiplier_2_out, multiplier_3_out, multiplier_4_out, multiplier_5_out,
       multiplier_6_out, multiplier_7_out, multiplier_8_out;

  Multiplier #(.width(32)) multiplier_1 (.a(in_1), .b(in_5), .out(multiplier_1_out));  // open: cin, cout
  Multiplier #(.width(32)) multiplier_2 (.a(in_2), .b(in_7), .out(multiplier_2_out));  // open: cin, cout
  Multiplier #(.width(32)) multiplier_3 (.a(in_1), .b(in_6), .out(multiplier_3_out));  // open: cin, cout
  Multiplier #(.width(32)) multiplier_4 (.a(in_2), .b(in_8), .out(multiplier_4_out));  // open: cin, cout
  Multiplier #(.width(32)) multiplier_5 (.a(in_3), .b(in_5), .out(multiplier_5_out));  // open: cin, cout
  Multiplier #(.width(32)) multiplier_6 (.a(in_4), .b(in_7), .out(multiplier_6_out));  // open: cin, cout
  Multiplier #(.width(32)) multiplier_7 (.a(in_3), .b(in_6), .out(multiplier_7_out));  // open: cin, cout
  Multiplier #(.width(32)) multiplier_8 (.a(in_4), .b(in_8), .out(multiplier_8_out));  // open: cin, cout
  Adder #(.width(32)) adder_1 (.a(multiplier_1_out), .b(multiplier_2_out), .out(out_9));  // open: cin, cout
  Adder #(.width(32)) adder_2 (.a(multiplier_3_out), .b(multiplier_4_out), .out(out_10));  // open: cin, cout
  Adder #(.width(32)) adder_3 (.a(multiplier_5_out), .b(multiplier_6_out), .out(out_11));  // open: cin, cout
  Adder #(.width(32)) adder_4 (.a(multiplier_7_out), .b(multiplier_8_out), .out(out_12));  // open: cin, cout

  // Other names for the same wires on the sheet: a11[31:0] = in_1; a12[31:0] = in_2; a21[31:0] = in_3;
  //   a22[31:0] = in_4; b11[31:0] = in_5; b12[31:0] = in_6; b21[31:0] = in_7; b22[31:0] = in_8
endmodule

module \技术逻辑  (
  input  [31:0] in_1,
  input  in_2,
  output n_low,
  output freeze
);

  wire clk, comparator_1_eq, init;
  wire [31:0] multiplexer_1_out, n, shifter_1_out;

  Counter #(.width(1), .max('h1)) counter_1 (.Q(init), .clk(clk), .clr(in_2));  // open: load, D, count, carry
  Clock clock_1 (.out(clk));
  Shifter #(.width(32), .shift("lr")) shifter_1 (.in(n), .\dist (5'b00001), .out(shifter_1_out));
  Comparator #(.width(32), .mode("unsigned")) comparator_1 (
    .a(n), .b({32{1'b0}}), .eq(comparator_1_eq));  // open: gt, lt
  Multiplexer #(.width(32)) multiplexer_1 (
    .in0(in_1), .in1(shifter_1_out), .out(multiplexer_1_out), .sel(init));  // open: en
  Bit_Extender #(.in_width(32), .out_width(1)) bit_extender_1 (.in(n), .out(n_low));
  Multiplexer multiplexer_2 (.in0(1'b0), .in1(comparator_1_eq), .out(freeze), .sel(init));  // open: en
  Register #(.width(32)) register_1 (.D(multiplexer_1_out), .Q(n), .clk(clk), .clr(in_2));  // open: en

  // Other names for the same wires on the sheet: clr = in_2; input[31:0] = in_1
endmodule
