// Logisim project 斐波那契第一次尝试.circ as structural Verilog: 3 circuits, main circuit 输入+判断次数
module \输入_判断次数  (
  input  [3:0] in_1,
  output out_2,
  output out_3
);

  wire clock_1_out, comparator_1_eq, comparator_1_gt;
  wire [3:0] adder_1_out, register_1_q, subtractor_1_out;

  // Probe on adder_1_out
  Register #(.width(4)) register_1 (.D(adder_1_out), .Q(register_1_q), .clk(clock_1_out));  // open: en, clr
  Clock clock_1 (.out(clock_1_out));
  Comparator #(.width(4), .mode("unsigned")) comparator_1 (
    .a(in_1), .b(subtractor_1_out), .gt(comparator_1_gt), .eq(comparator_1_eq));  // open: lt
  Adder #(.width(4)) adder_1 (.a(register_1_q), .b(4'b0001), .out(adder_1_out));  // open: cin, cout
  or or_1 (out_2, comparator_1_gt, comparator_1_eq);
  // Probe on subtractor_1_out
  Subtractor #(.width(4)) subtractor_1 (.a(adder_1_out), .b(4'b0001), .out(subtractor_1_out));  // open: bin, bout
  Comparator #(.width(4), .mode("unsigned")) comparator_2 (
    .a(4'b0000), .b(subtractor_1_out), .eq(out_3));  // open: gt, lt
endmodule

module \斐波那契加法  (
  input  in_1,
  input  in_2
);

  wire clock_1_out, F;
  wire [3:0] adder_1_out, adder_2_out, and_1_out, bit_extender_1_out, register_1_q;

  // Probe on adder_2_out
  Register #(.width(4)) register_1 (.D(adder_2_out), .en(in_1), .Q(register_1_q), .clk(clock_1_out));  // open: clr
  Clock clock_1 (.out(clock_1_out));
  // Probe on register_1_q
  // Probe on register_1_q
  Comparator #(.width(4), .mode("unsigned")) comparator_1 (.a(4'b0000), .b(register_1_q), .eq(F));  // open: gt, lt
  // Probe on adder_2_out
  assign and_1_out = 4'b0001 & bit_extender_1_out;  // AND_Gate and_1, 4 bits wide
  assign bit_extender_1_out = {{3{1'b0}}, F};  // Bit_Extender bit_extender_1
  // Probe on adder_1_out
  Adder #(.width(4)) adder_1 (.a(register_1_q), .b(and_1_out), .out(adder_1_out));  // open: cin, cout
  Adder #(.width(4)) adder_2 (.a(adder_1_out), .b(adder_2_out), .out(adder_2_out));  // open: cin, cout
endmodule

module test (
  input  [7:0] in_1,
  input  [7:0] in_2,
  input  in_3,
  output [7:0] out_4
);

  Adder adder_1 (.a(in_1), .b(in_2), .out(out_4), .cout(in_3));  // open: cin
endmodule
