// Logisim project 斐波那契第二次尝试.circ as structural Verilog: 3 circuits, main circuit core
module core (
  input  [2:0] in_1,
  output out_2
);

  wire clock_1_out;
  wire [3:0] bit_extender_1_out, counter_1_q;

  assign bit_extender_1_out = {{1{1'b0}}, in_1};  // Bit_Extender bit_extender_1
  Counter #(.width(4), .max('hf)) counter_1 (.Q(counter_1_q), .clk(clock_1_out));  // open: load, D, count, carry, clr
  Clock clock_1 (.out(clock_1_out));
  Comparator #(.width(4), .mode("unsigned")) comparator_1 (
    .a(bit_extender_1_out), .b(counter_1_q), .lt(out_2));  // open: gt, eq
endmodule

module \计算值  (
  input  in_1,
  output [3:0] out_2,
  output [3:0] out_3
);

  wire clock_1_out, clock_2_out, clock_3_out, comparator_1_gt, flag;
  wire [3:0] adder_1_out, counter_1_q, multiplexer_1_out;

  Clock clock_1 (.out(clock_1_out));
  not not_1 (flag, in_1);
  Counter #(.width(4), .max('hf)) counter_1 (.Q(counter_1_q), .clk(clock_1_out));  // open: load, D, count, carry, clr
  Comparator #(.width(4), .mode("unsigned")) comparator_1 (
    .a(counter_1_q), .b(4'b0000), .gt(comparator_1_gt));  // open: eq, lt
  Multiplexer #(.width(4)) multiplexer_1 (
    .in0(4'b0001), .in1(out_3), .out(multiplexer_1_out), .sel(comparator_1_gt));  // open: en
  Adder #(.width(4)) adder_1 (.a(out_2), .b(out_3), .out(adder_1_out));  // open: cin, cout
  Clock clock_2 (.out(clock_2_out));
  Register #(.width(4)) register_1 (.D(multiplexer_1_out), .en(flag), .Q(out_2), .clk(clock_2_out));  // open: clr
  Register #(.width(4)) register_2 (.D(adder_1_out), .en(flag), .Q(out_3), .clk(clock_3_out));  // open: clr
  Clock clock_3 (.out(clock_3_out));

  // Other names for the same wires on the sheet: before[3:0] = out_2; now[3:0] = out_3
endmodule

module main (
  input  [2:0] in_1,
  output [3:0] out_2
);

  wire core_1_out_2;

  core core_1 (.in_1(in_1), .out_2(core_1_out_2));
  \计算值  \u_计算值_1  (.in_1(core_1_out_2), .out_3(out_2));  // open: out_2
endmodule
