// Logisim project 递推数列练习.circ as structural Verilog: 2 circuits, main circuit main
module main (
  input  [7:0] in_1,
  output [31:0] out_2
);

  \计算逻辑  \u_计算逻辑_1  (.in_1(in_1), .out_2(out_2));
endmodule

module \计算逻辑  (
  input  [7:0] in_1,
  output [31:0] out_2
);

  wire and_1_out, clk, comparator_1_eq, comparator_3_eq, comparator_3_gt, flag1, flag2, not_3_out, or_1_out,
       \计数器是否工作 ;
  wire [7:0] \目前已过周期数 ;
  wire [31:0] adder_1_out, and_2_out, f_x, f_x_1, f_x_2, f_x_3, multiplexer_1_out, multiplexer_2_out,
       multiplexer_3_out, multiplexer_4_out;

  Clock clock_1 (.out(clk));
  Comparator #(.mode("unsigned")) comparator_1 (.a(in_1), .b({8{1'b0}}), .eq(comparator_1_eq));  // open: gt, lt
  not not_1 (\计数器是否工作 , comparator_1_eq);
  Counter counter_1 (.count(and_1_out), .Q(\目前已过周期数 ), .clk(clk));  // open: load, D, carry, clr
  and and_1 (and_1_out, \计数器是否工作 , flag2);
  Comparator comparator_2 (.a(\目前已过周期数 ), .b(8'h4), .lt(flag1));  // open: gt, eq
  Comparator comparator_3 (.a(\目前已过周期数 ), .b(in_1), .gt(comparator_3_gt), .eq(comparator_3_eq));  // open: lt
  or or_1 (or_1_out, comparator_3_gt, comparator_3_eq);
  not not_2 (flag2, or_1_out);
  assign and_2_out = f_x_3 & f_x_2;  // AND_Gate and_2, 32 bits wide
  Adder #(.width(32)) adder_1 (.a(and_2_out), .b(f_x_1), .out(adder_1_out));  // open: cin, cout
  Multiplexer #(.width(32)) multiplexer_1 (.in0(f_x_2), .in1(32'h1), .out(multiplexer_1_out), .sel(flag1));  // open: en
  Multiplexer #(.width(32)) multiplexer_2 (.in0(f_x_1), .in1(32'h1), .out(multiplexer_2_out), .sel(flag1));  // open: en
  Multiplexer #(.width(32)) multiplexer_3 (.in0(f_x), .in1(32'h1), .out(multiplexer_3_out), .sel(flag1));  // open: en
  Multiplexer #(.width(32)) multiplexer_4 (
    .in0(adder_1_out), .in1(32'h1), .out(multiplexer_4_out), .sel(flag1));  // open: en
  Register #(.width(32)) \f_x_3_寄存器  (.D(multiplexer_1_out), .en(flag2), .Q(f_x_3), .clk(clk));  // open: clr
  Register #(.width(32)) \f_x_2_寄存器  (.D(multiplexer_2_out), .en(flag2), .Q(f_x_2), .clk(clk));  // open: clr
  Register #(.width(32)) \f_x_1_寄存器  (.D(multiplexer_3_out), .en(flag2), .Q(f_x_1), .clk(clk));  // open: clr
  Register #(.width(32)) \f_x_寄存器  (.D(multiplexer_4_out), .en(flag2), .Q(f_x), .clk(clk));  // open: clr
  Multiplexer #(.width(32)) multiplexer_5 (.in0({32{1'b0}}), .in1(f_x), .out(out_2), .sel(not_3_out));  // open: en
  not not_3 (not_3_out, flag2);

  // Other names for the same wires on the sheet: 周期数[7:0] = in_1
endmodule
